// Logisim project microprocesador.circ as structural Verilog: 14 circuits, main circuit Data Path
module Control_Unit (
  input  nop,
  input  \and ,
  input  xori,
  input  bltz,
  input  add,
  input  \or ,
  input  lw,
  input  j,
  input  sub,
  input  \nor ,
  input  sw,
  input  jr,
  input  mul,
  input  \xor ,
  input  pop,
  input  mfhi,
  input  mulu,
  input  addi,
  input  push,
  input  mflo,
  input  div,
  input  slti,
  input  beq,
  input  halt,
  input  divu,
  input  sltiu,
  input  bne,
  input  tty,
  input  slt,
  input  andi,
  input  blez,
  input  rnd,
  input  sltu,
  input  ori,
  input  bgtz,
  input  kbd,
  input  Reset,
  input  Clock,
  input  SP_0,
  input  RT__0,
  input  WT__0,
  input  First_Instruction,
  input  KBD_Avalaible,
  output ALUSB,
  output [2:0] Selector_Data_Input,
  output [1:0] Stack_Point_Selector,
  output CURW,
  output [2:0] Branch_Control_Selector,
  output Enabled_PC,
  output CS,
  output [1:0] Memory_Manager_Selector,
  output SRT,
  output SWT,
  output minus_RW,
  output Enable_Inst,
  output KBD_Enable,
  output TTY_Enable
);

  wire ALUSB0, ALUSB1, BCS0_0, BCS0_1, BCS0_2, BCS1_0, BCS2_0, demultiplexer_1_out0, demultiplexer_1_out1,
       demultiplexer_2_out0, demultiplexer_2_out1, demultiplexer_3_out1, demultiplexer_4_out0,
       demultiplexer_4_out1, demultiplexer_5_out0, demultiplexer_6_out1, demultiplexer_7_out0,
       demultiplexer_7_out1, demultiplexer_9_out0, demultiplexer_9_out1, demultiplexer_11_out0,
       demultiplexer_11_out1, demultiplexer_12_out0, demultiplexer_12_out1, demultiplexer_13_out0,
       demultiplexer_14_out0, demultiplexer_14_out1, demultiplexer_15_out1, demultiplexer_16_out0,
       demultiplexer_16_out1, demultiplexer_17_out0, demultiplexer_17_out1, demultiplexer_18_out0,
       demultiplexer_18_out1, demultiplexer_19_out0, demultiplexer_19_out1, demultiplexer_20_out1,
       demultiplexer_21_out1, demultiplexer_22_out0, demultiplexer_22_out1, demultiplexer_23_out0,
       demultiplexer_23_out1, demultiplexer_24_out0, demultiplexer_24_out1, demultiplexer_25_out0,
       demultiplexer_25_out1, demultiplexer_27_out0, demultiplexer_27_out1, demultiplexer_28_out1,
       demultiplexer_29_out1, demultiplexer_30_out0, demultiplexer_31_out0, demultiplexer_33_out1,
       demultiplexer_37_out1, demultiplexer_38_out1, demultiplexer_41_out0, demultiplexer_41_out1,
       demultiplexer_42_out0, demultiplexer_43_out0, demultiplexer_44_out1, demultiplexer_45_out0,
       demultiplexer_45_out1, demultiplexer_46_out0, demultiplexer_46_out1, demultiplexer_47_out0,
       demultiplexer_47_out1, demultiplexer_48_out1, demultiplexer_49_out1, demultiplexer_50_out1,
       demultiplexer_51_out1, demultiplexer_52_out1, En_Inst0, En_Inst1, En_PC5, End_2_q, End_5_q, End_6_q,
       End_7_q, End_8_q, end_ALU, End_BCU, End_Instruction_q, end_MM, End_q, End_RF, End_RT, End_RT_2_q,
       End_RT_q, End_WT, End_WT_2_q, End_WT_q, F, First_Instruction_q, Idle_2_q, Idle_4_q, Idle_5_q,
       Idle_6_q, Idle_7_q, Idle_8_q, Idle_9_q, minus_RW1, MMS0_0, MMS0_2, MMS1_1, not_2_out, not_3_out,
       not_4_out, not_5_out, not_6_out, not_7_out, not_8_out, not_9_out, not_10_out, not_11_out, not_12_out,
       not_13_out, not_14_out, not_15_out, o0, o1, o2, o3, o4, o5, o6, o7, o8, o9, o10, or_1_out, or_2_out,
       or_3_out, or_6_out, or_7_out, or_8_out, or_10_out, or_11_out, or_15_out, or_16_out, or_17_out,
       or_18_out, or_23_out, or_25_out, or_26_out, or_27_out, or_28_out, or_29_out, or_30_out, or_31_out,
       or_32_out, or_33_out, or_34_out, or_35_out, or_36_out, or_37_out, or_38_out, or_39_out, or_40_out,
       or_41_out, or_42_out, or_43_out, or_44_out, or_45_out, or_46_out, or_47_out, or_48_out, or_49_out,
       or_51_out, or_55_out, or_56_out, or_58_out, PC_q, Push_Write_Time_q, Read_Time_2_q, rst, RW0, RW1,
       SDI0_0, SDI0_1, SRT0, SRT1, SRT2, SRT3, SSP0_0, start, Update_Values_q, wait_branch, Wait_MM_2_q,
       Wait_MM_3_q, Wait_MM_4_q, Wait_MM_5_q, Wait_MM_q, wait_rf, Wr, Write_Time_q;

  or or_1 (or_1_out, end_MM, Reset);
  or or_2 (or_2_out, Reset, halt);
  D_Flip_Flop Idle (.clk(Clock), .D(Idle_2_q), .Q(start));  // open: Qn, preset, en, reset
  D_Flip_Flop Idle_2 (.clk(Clock), .D(or_1_out), .Q(Idle_2_q));  // open: Qn, preset, en, reset
  D_Flip_Flop Idle_3 (.clk(Clock), .D(or_2_out), .Q(rst));  // open: Qn, preset, en, reset
  or or_3 (or_3_out, demultiplexer_1_out0, demultiplexer_50_out1);
  or or_4 (Memory_Manager_Selector[0], MMS0_0, MMS0_2, ALUSB1);
  or or_5 (Memory_Manager_Selector[1], minus_RW1, MMS1_1);
  D_Flip_Flop Idle_4 (.clk(Clock), .D(or_6_out), .Q(Idle_4_q), .preset(rst));  // open: Qn, en, reset
  or or_6 (or_6_out, demultiplexer_2_out0, demultiplexer_52_out1);
  or or_7 (or_7_out, demultiplexer_4_out0, demultiplexer_51_out1);
  not not_1 (CS, demultiplexer_1_out0);
  Demultiplexer #(.enable("false")) demultiplexer_1 (
    .out0(demultiplexer_1_out0), .out1(demultiplexer_1_out1), .in(Idle_5_q), .sel(start));
  D_Flip_Flop Idle_5 (.clk(Clock), .D(or_3_out), .Q(Idle_5_q), .preset(rst));  // open: Qn, en, reset
  Demultiplexer #(.enable("false")) demultiplexer_2 (
    .out0(demultiplexer_2_out0), .out1(demultiplexer_2_out1), .in(Idle_4_q), .sel(start));
  Demultiplexer #(.enable("false")) demultiplexer_3 (.out0(o7), .out1(demultiplexer_3_out1), .in(F), .sel(not_2_out));
  not not_2 (not_2_out, or_8_out);
  or or_8 (or_8_out, add, sub, mul, mulu, div, divu, slt, sltu, \and , \or , \nor , \xor , addi, slti, sltiu, andi, ori, xori);
  Demultiplexer #(.enable("false")) demultiplexer_4 (
    .out0(demultiplexer_4_out0), .out1(demultiplexer_4_out1), .in(Idle_6_q), .sel(start));
  D_Flip_Flop Idle_6 (.clk(Clock), .D(or_7_out), .Q(Idle_6_q), .preset(rst));  // open: Qn, en, reset
  Demultiplexer #(.enable("false")) demultiplexer_5 (
    .out0(demultiplexer_5_out0), .out1(En_Inst1), .in(demultiplexer_1_out1), .sel(not_3_out));
  not not_3 (not_3_out, First_Instruction);
  or or_9 (Enable_Inst, En_Inst0, En_Inst1);
  D_Flip_Flop Wait_MM (.clk(Clock), .D(or_10_out), .Q(Wait_MM_q), .reset(rst));  // open: Qn, preset, en
  or or_10 (or_10_out, demultiplexer_7_out0, demultiplexer_2_out1);
  Demultiplexer #(.enable("false")) demultiplexer_6 (
    .out0(o8), .out1(demultiplexer_6_out1), .in(demultiplexer_3_out1), .sel(not_4_out));
  not not_4 (not_4_out, rnd);
  or or_11 (or_11_out, demultiplexer_9_out0, demultiplexer_4_out1);
  or or_12 (Branch_Control_Selector[0], BCS0_0, BCS0_2, BCS0_1);
  or or_13 (Branch_Control_Selector[1], BCS1_0, BCS0_1);
  or or_14 (Branch_Control_Selector[2], BCS2_0, BCS0_2);
  D_Flip_Flop u_First_Instruction (
    .clk(Clock), .D(or_15_out), .Q(First_Instruction_q), .reset(rst));  // open: Qn, preset, en
  or or_15 (or_15_out, SRT0, demultiplexer_5_out0);
  or or_16 (or_16_out, En_Inst0, En_Inst1);
  or or_17 (or_17_out, demultiplexer_11_out0, demultiplexer_45_out1);
  or or_18 (or_18_out, demultiplexer_12_out0, demultiplexer_46_out1);
  Demultiplexer #(.enable("false")) demultiplexer_7 (
    .out0(demultiplexer_7_out0), .out1(demultiplexer_7_out1), .in(Wait_MM_q), .sel(wait_rf));
  Demultiplexer #(.enable("false")) demultiplexer_8 (
    .out0(o9), .out1(o10), .in(demultiplexer_6_out1), .sel(KBD_Avalaible));
  D_Flip_Flop Wait_MM_2 (.clk(Clock), .D(or_11_out), .Q(Wait_MM_2_q), .reset(rst));  // open: Qn, preset, en
  Demultiplexer #(.enable("false")) demultiplexer_9 (
    .out0(demultiplexer_9_out0), .out1(demultiplexer_9_out1), .in(Wait_MM_2_q), .sel(wait_branch));
  Demultiplexer #(.enable("false")) demultiplexer_10 (
    .out0(SRT0), .out1(En_Inst0), .in(First_Instruction_q), .sel(RT__0));
  D_Flip_Flop Current_Instruction (.clk(Clock), .D(or_16_out), .Q(wait_rf), .reset(rst));  // open: Qn, preset, en
  or or_19 (Wr, sw, push);
  or or_20 (SRT, SRT0, SRT1, SRT2, SRT3);
  or or_21 (SWT, ALUSB1, minus_RW1);
  or or_22 (minus_RW, ALUSB1, minus_RW1);
  D_Flip_Flop Idle_7 (.clk(Clock), .D(or_17_out), .Q(Idle_7_q), .preset(rst));  // open: Qn, en, reset
  Demultiplexer #(.enable("false")) demultiplexer_11 (
    .out0(demultiplexer_11_out0), .out1(demultiplexer_11_out1), .in(Idle_7_q), .sel(start));
  Demultiplexer #(.enable("false")) demultiplexer_12 (
    .out0(demultiplexer_12_out0), .out1(demultiplexer_12_out1), .in(Idle_8_q), .sel(start));
  D_Flip_Flop Idle_8 (.clk(Clock), .D(or_18_out), .Q(Idle_8_q), .preset(rst));  // open: Qn, en, reset
  or or_23 (or_23_out, add, sub, mul, mulu, div, divu, slt, sltu, \and , \or , \nor , \xor , beq, bne, blez, bgtz, bltz);
  Demultiplexer #(.enable("false")) demultiplexer_13 (
    .out0(demultiplexer_13_out0), .out1(o1), .in(demultiplexer_14_out0), .sel(SP_0));
  Demultiplexer #(.enable("false")) demultiplexer_14 (
    .out0(demultiplexer_14_out0), .out1(demultiplexer_14_out1), .in(demultiplexer_7_out1), .sel(not_5_out));
  not not_5 (not_5_out, pop);
  Demultiplexer #(.enable("false")) demultiplexer_15 (
    .out0(BCS0_0), .out1(demultiplexer_15_out1), .in(demultiplexer_9_out1), .sel(not_6_out));
  not not_6 (not_6_out, beq);
  // OR_Gate or_24 has open pins: in0=end_MM, in1=First_Instruction, in2=En_Inst0, out=open
  Demultiplexer #(.enable("false")) demultiplexer_16 (
    .out0(demultiplexer_16_out0), .out1(demultiplexer_16_out1), .in(demultiplexer_17_out0), .sel(Wr));
  Demultiplexer #(.enable("false")) demultiplexer_17 (
    .out0(demultiplexer_17_out0), .out1(demultiplexer_17_out1), .in(wait_rf), .sel(or_25_out));
  or or_25 (or_25_out, lw, pop);
  Demultiplexer #(.enable("false")) demultiplexer_18 (
    .out0(demultiplexer_18_out0), .out1(demultiplexer_18_out1), .in(demultiplexer_17_out1), .sel(pop));
  or or_26 (or_26_out, demultiplexer_23_out0, demultiplexer_11_out1);
  or or_27 (or_27_out, demultiplexer_24_out0, demultiplexer_12_out1);
  or or_28 (or_28_out, demultiplexer_25_out0, demultiplexer_49_out1);
  or or_29 (or_29_out, SDI0_1, demultiplexer_19_out0);
  Demultiplexer #(.enable("false")) demultiplexer_19 (
    .out0(demultiplexer_19_out0), .out1(demultiplexer_19_out1), .in(demultiplexer_14_out1), .sel(not_7_out));
  not not_7 (not_7_out, lw);
  Demultiplexer #(.enable("false")) demultiplexer_20 (
    .out0(SSP0_0), .out1(demultiplexer_20_out1), .in(demultiplexer_19_out1), .sel(not_8_out));
  not not_8 (not_8_out, push);
  Demultiplexer #(.enable("false")) demultiplexer_21 (
    .out0(BCS1_0), .out1(demultiplexer_21_out1), .in(demultiplexer_15_out1), .sel(not_9_out));
  not not_9 (not_9_out, bne);
  Demultiplexer #(.enable("false")) demultiplexer_22 (
    .out0(demultiplexer_22_out0), .out1(demultiplexer_22_out1), .in(demultiplexer_16_out1), .sel(push));
  or or_30 (or_30_out, SRT2, demultiplexer_18_out0);
  Demultiplexer #(.enable("false")) demultiplexer_23 (
    .out0(demultiplexer_23_out0), .out1(demultiplexer_23_out1), .in(Wait_MM_3_q), .sel(or_37_out));
  D_Flip_Flop Wait_MM_3 (.clk(Clock), .D(or_26_out), .Q(Wait_MM_3_q), .reset(rst));  // open: Qn, preset, en
  D_Flip_Flop Wait_MM_4 (.clk(Clock), .D(or_27_out), .Q(Wait_MM_4_q), .reset(rst));  // open: Qn, preset, en
  Demultiplexer #(.enable("false")) demultiplexer_24 (
    .out0(demultiplexer_24_out0), .out1(demultiplexer_24_out1), .in(Wait_MM_4_q), .sel(or_31_out));
  or or_31 (or_31_out, end_MM, ~First_Instruction, En_Inst0);  // OR_Gate
  D_Flip_Flop Idle_9 (.clk(Clock), .D(or_28_out), .Q(Idle_9_q), .preset(rst));  // open: Qn, en, reset
  Demultiplexer #(.enable("false")) demultiplexer_25 (
    .out0(demultiplexer_25_out0), .out1(demultiplexer_25_out1), .in(Idle_9_q), .sel(start));
  D_Flip_Flop u_End_RT (.clk(Clock), .D(or_32_out), .Q(End_RT_q), .reset(rst));  // open: Qn, preset, en
  or or_32 (or_32_out, SDI0_0, demultiplexer_13_out0);
  D_Flip_Flop End_RT_2 (.clk(Clock), .D(or_29_out), .Q(End_RT_2_q), .reset(rst));  // open: Qn, preset, en
  Demultiplexer #(.enable("false")) demultiplexer_26 (.out0(SDI0_1), .out1(o2), .in(End_RT_2_q), .sel(End_RT));
  Demultiplexer #(.enable("false")) demultiplexer_27 (
    .out0(demultiplexer_27_out0), .out1(demultiplexer_27_out1), .in(demultiplexer_20_out1), .sel(not_10_out));
  not not_10 (not_10_out, sw);
  Demultiplexer #(.enable("false")) demultiplexer_28 (
    .out0(BCS0_1), .out1(demultiplexer_28_out1), .in(demultiplexer_21_out1), .sel(not_11_out));
  not not_11 (not_11_out, blez);
  Demultiplexer #(.enable("false")) demultiplexer_29 (
    .out0(BCS2_0), .out1(demultiplexer_29_out1), .in(demultiplexer_28_out1), .sel(not_12_out));
  not not_12 (not_12_out, bgtz);
  or or_33 (or_33_out, wait_branch, demultiplexer_16_out0, End_WT, End_RT);
  or or_34 (or_34_out, ALUSB1, demultiplexer_22_out0);
  or or_35 (or_35_out, minus_RW1, demultiplexer_22_out1);
  D_Flip_Flop Read_Time (.clk(Clock), .D(or_30_out), .Q(MMS0_2), .reset(rst));  // open: Qn, preset, en
  D_Flip_Flop Pop_Read_Time (.clk(Clock), .D(or_36_out), .Q(MMS1_1), .reset(rst));  // open: Qn, preset, en
  or or_36 (or_36_out, SRT3, demultiplexer_18_out1);
  Demultiplexer #(.enable("false")) demultiplexer_30 (
    .out0(demultiplexer_30_out0), .out1(KBD_Enable), .in(demultiplexer_23_out1), .sel(kbd));
  or or_37 (or_37_out, end_MM, ~First_Instruction, En_Inst0);  // OR_Gate
  Demultiplexer #(.enable("false")) demultiplexer_31 (
    .out0(demultiplexer_31_out0), .out1(TTY_Enable), .in(demultiplexer_24_out1), .sel(tty));
  or or_38 (or_38_out, demultiplexer_41_out0, demultiplexer_25_out1);
  Demultiplexer #(.enable("false")) demultiplexer_32 (.out0(SDI0_0), .out1(o0), .in(End_RT_q), .sel(End_RT));
  D_Flip_Flop u_End_WT (.clk(Clock), .D(or_39_out), .Q(End_WT_q), .reset(rst));  // open: Qn, preset, en
  or or_39 (or_39_out, demultiplexer_42_out0, SSP0_0);
  D_Flip_Flop End_WT_2 (.clk(Clock), .D(or_40_out), .Q(End_WT_2_q), .reset(rst));  // open: Qn, preset, en
  or or_40 (or_40_out, demultiplexer_43_out0, demultiplexer_27_out0);
  Demultiplexer #(.enable("false")) demultiplexer_33 (
    .out0(o5), .out1(demultiplexer_33_out1), .in(demultiplexer_27_out1), .sel(not_13_out));
  not not_13 (not_13_out, mfhi);
  Demultiplexer #(.enable("false")) demultiplexer_34 (
    .out0(o6), .out1(F), .in(demultiplexer_33_out1), .sel(not_14_out));
  not not_14 (not_14_out, mflo);
  Demultiplexer #(.enable("false")) demultiplexer_35 (
    .out0(BCS0_2), .out1(En_PC5), .in(demultiplexer_29_out1), .sel(not_15_out));
  not not_15 (not_15_out, bltz);
  Demultiplexer #(.enable("false")) demultiplexer_36 (.out0(wait_branch), .out1(MMS0_0), .in(PC_q), .sel(End_BCU));
  D_Flip_Flop PC (.clk(Clock), .D(or_33_out), .Q(PC_q), .reset(rst));  // open: Qn, preset, en
  D_Flip_Flop Write_Time (.clk(Clock), .D(or_34_out), .Q(Write_Time_q), .reset(rst));  // open: Qn, preset, en
  Demultiplexer #(.enable("false")) demultiplexer_37 (
    .out0(ALUSB1), .out1(demultiplexer_37_out1), .in(Write_Time_q), .sel(WT__0));
  D_Flip_Flop Push_Write_Time (.clk(Clock), .D(or_35_out), .Q(Push_Write_Time_q), .reset(rst));  // open: Qn, preset, en
  Demultiplexer #(.enable("false")) demultiplexer_38 (
    .out0(minus_RW1), .out1(demultiplexer_38_out1), .in(Push_Write_Time_q), .sel(WT__0));
  Demultiplexer #(.enable("false")) demultiplexer_39 (.out0(SRT2), .out1(RW1), .in(MMS0_2), .sel(RT__0));
  Demultiplexer #(.enable("false")) demultiplexer_40 (.out0(SRT3), .out1(RW0), .in(MMS1_1), .sel(RT__0));
  Demultiplexer #(.enable("false")) demultiplexer_41 (
    .out0(demultiplexer_41_out0), .out1(demultiplexer_41_out1), .in(Wait_MM_5_q), .sel(wait_rf));
  D_Flip_Flop Wait_MM_5 (.clk(Clock), .D(or_38_out), .Q(Wait_MM_5_q), .reset(rst));  // open: Qn, preset, en
  Demultiplexer #(.enable("false")) demultiplexer_42 (
    .out0(demultiplexer_42_out0), .out1(o3), .in(End_WT_q), .sel(End_WT));
  Demultiplexer #(.enable("false")) demultiplexer_43 (
    .out0(demultiplexer_43_out0), .out1(o4), .in(End_WT_2_q), .sel(End_WT));
  or or_41 (or_41_out, demultiplexer_45_out0, demultiplexer_30_out0, KBD_Enable);
  or or_42 (or_42_out, demultiplexer_46_out0, demultiplexer_31_out0, TTY_Enable);
  Demultiplexer #(.enable("false")) demultiplexer_44 (
    .out0(ALUSB0), .out1(demultiplexer_44_out1), .in(demultiplexer_41_out1), .sel(or_23_out));
  or or_43 (or_43_out, demultiplexer_47_out0, BCS0_0, BCS1_0, BCS0_1, BCS2_0, BCS0_2, En_PC5);
  or or_44 (or_44_out, SRT1, MMS0_0);
  or or_45 (or_45_out, End_WT, demultiplexer_37_out1, demultiplexer_38_out1);
  or or_46 (or_46_out, End_RT, RW1, RW0);
  Demultiplexer #(.enable("false")) demultiplexer_45 (
    .out0(demultiplexer_45_out0), .out1(demultiplexer_45_out1), .in(End_q), .sel(start));
  D_Flip_Flop End (.clk(Clock), .D(or_41_out), .Q(End_q), .reset(rst));  // open: Qn, preset, en
  D_Flip_Flop End_2 (.clk(Clock), .D(or_42_out), .Q(End_2_q), .reset(rst));  // open: Qn, preset, en
  Demultiplexer #(.enable("false")) demultiplexer_46 (
    .out0(demultiplexer_46_out0), .out1(demultiplexer_46_out1), .in(End_2_q), .sel(start));
  D_Flip_Flop End_Instruction (.clk(Clock), .D(or_43_out), .Q(End_Instruction_q), .reset(rst));  // open: Qn, preset, en
  Demultiplexer #(.enable("false")) demultiplexer_47 (
    .out0(demultiplexer_47_out0), .out1(demultiplexer_47_out1), .in(End_Instruction_q), .sel(End_RF));
  Demultiplexer #(.enable("false")) demultiplexer_48 (
    .out0(SRT1), .out1(demultiplexer_48_out1), .in(Read_Time_2_q), .sel(RT__0));
  D_Flip_Flop Read_Time_2 (.clk(Clock), .D(or_44_out), .Q(Read_Time_2_q), .reset(rst));  // open: Qn, preset, en
  D_Flip_Flop End_3 (.clk(Clock), .D(or_45_out), .Q(End_WT), .reset(or_47_out));  // open: Qn, preset, en
  or or_47 (or_47_out, MMS0_0, rst);
  D_Flip_Flop End_4 (.clk(Clock), .D(or_46_out), .Q(End_RT), .reset(or_48_out));  // open: Qn, preset, en
  or or_48 (or_48_out, MMS0_0, rst);
  D_Flip_Flop End_5 (.clk(Clock), .D(or_49_out), .Q(End_5_q), .reset(rst));  // open: Qn, preset, en
  or or_49 (or_49_out, end_ALU, ALUSB0, demultiplexer_44_out1);
  or or_50 (ALUSB, ALUSB0, ALUSB1);
  or or_51 (or_51_out, o0, o2, o5, o6, o7, o8, o9, o10);
  or or_52 (Selector_Data_Input[0], SDI0_0, SDI0_1, o5, o9);
  or or_53 (Selector_Data_Input[1], SDI0_0, SDI0_1, o8, o7);
  or or_54 (Selector_Data_Input[2], o8, o9, o10);
  or or_55 (or_55_out, End_BCU, demultiplexer_47_out1);
  or or_56 (or_56_out, end_MM, demultiplexer_48_out1);
  Demultiplexer #(.enable("false")) demultiplexer_49 (
    .out0(end_ALU), .out1(demultiplexer_49_out1), .in(End_5_q), .sel(start));
  D_Flip_Flop Update_Values (.clk(Clock), .D(or_51_out), .Q(Update_Values_q), .reset(rst));  // open: Qn, preset, en
  D_Flip_Flop End_6 (.clk(Clock), .D(or_55_out), .Q(End_6_q), .reset(rst));  // open: Qn, preset, en
  or or_57 (Enabled_PC, BCS0_0, BCS1_0, BCS0_1, BCS2_0, BCS0_2, En_PC5);
  D_Flip_Flop End_7 (.clk(Clock), .D(or_56_out), .Q(End_7_q), .reset(rst));  // open: Qn, preset, en
  Demultiplexer #(.enable("false")) demultiplexer_50 (
    .out0(end_MM), .out1(demultiplexer_50_out1), .in(End_7_q), .sel(start));
  or or_58 (or_58_out, End_RF, Update_Values_q, o1, o3, o4);
  or or_59 (Stack_Point_Selector[0], SSP0_0, rst);
  or or_60 (Stack_Point_Selector[1], o0, SSP0_0);
  or or_61 (CURW, RW0, RW1, o5, o6, o7, o8, o9, o10);
  Demultiplexer #(.enable("false")) demultiplexer_51 (
    .out0(End_BCU), .out1(demultiplexer_51_out1), .in(End_6_q), .sel(start));
  D_Flip_Flop End_8 (.clk(Clock), .D(or_58_out), .Q(End_8_q), .reset(rst));  // open: Qn, preset, en
  Demultiplexer #(.enable("false")) demultiplexer_52 (
    .out0(End_RF), .out1(demultiplexer_52_out1), .in(End_8_q), .sel(start));

  // Other names for the same wires on the sheet: BCS[2:0] = Branch_Control_Selector; clk = Clock;
  //   En_Inst = Enable_Inst; En_PC = Enabled_PC; En_PC0 = BCS0_0; En_PC1 = BCS1_0; BCS1_1 = BCS0_1; En_PC2 = BCS0_1;
  //   En_PC3 = BCS2_0; BCS2_1 = BCS0_2; En_PC4 = BCS0_2; End_FI = En_Inst0; FI = First_Instruction;
  //   KBD_Available = KBD_Avalaible; SSP1_0 = o0; RW2 = o5; SDI0_2 = o5; RW3 = o6; RW4 = o7; SDI1_2 = o7; RW5 = o8;
  //   SDI1_3 = o8; SDI2_0 = o8; RW6 = o9; SDI0_3 = o9; SDI2_1 = o9; RW7 = o10; SDI2_2 = o10; SSP0_1 = rst;
  //   rst_RT = MMS0_0; rst_WT = MMS0_0; RW = CURW; SDI[2:0] = Selector_Data_Input; SDI1_0 = SDI0_0; SDI1_1 = SDI0_1;
  //   SSP[1:0] = Stack_Point_Selector; SSP1_1 = SSP0_0; minus_RW0 = ALUSB1; MMS0_1 = ALUSB1; SWT0 = ALUSB1;
  //   MMS1_0 = minus_RW1; SWT1 = minus_RW1

  // Notes on the sheet:
  //   Control Unit Register File
  //   Control Unit TTY
  //   Control Unit Memory Manager
  //   Control Unit Keyboard
  //   Control Unit Branch Control
  //   Control Unit ALU
endmodule

module Data_Path (
  input  Clock,
  input  [6:0] KBD_DATA,
  input  KBD_Avail,
  input  Reset,
  input  [31:0] In_RAM0,
  input  [1:0] Memory_Selector,
  input  [31:0] In_RAM1,
  input  [2:0] Selector_Data_Input,
  input  [1:0] Stack_Point_Selector,
  input  ALUSB,
  input  [31:0] In_RAM2,
  input  [31:0] In_RAM3,
  input  Enabled_PC,
  input  [2:0] Branch_Control_Selector,
  input  [3:0] RT,
  input  [3:0] WT,
  input  SRT,
  input  SWT,
  input  CURW,
  input  Enable_Instruction,
  output [6:0] TTY_DATA,
  output KBD_Clear,
  output TTY_Enable,
  output out_24,
  output WT__0,
  output RT__0,
  output nop,
  output add,
  output \and ,
  output xori,
  output bltz,
  output [31:0] Out_RAM0,
  output First_Instruction,
  output \or ,
  output lw,
  output j,
  output sub,
  output \nor ,
  output sw,
  output jr,
  output mul,
  output \xor ,
  output pop,
  output mfhi,
  output [31:0] Out_RAM1,
  output Stop,
  output mulu,
  output addi,
  output push,
  output mflo,
  output slti,
  output beq,
  output halt,
  output div,
  output sltiu,
  output bne,
  output tty,
  output [31:0] Out_RAM2,
  output divu,
  output andi,
  output blez,
  output rnd,
  output slt,
  output ori,
  output bgtz,
  output kbd,
  output [31:0] Out_RAM3,
  output sltu,
  output [15:0] Addr,
  output [3:0] Mask
);

  wire A_B, A_B_t, A_B_t_t, ENHL, jmp, multiplexer_2_out, or_1_out, or_2_out, or_3_out, or_4_out, PreRW, RW;
  wire [3:0] Op;
  wire [4:0] DA, SA, SB;
  wire [31:0] B, branch_control_1_out_9, F, Hi, Instruction_q, K, KBD_t, Lo, mem, multiplexer_1_out,
       multiplexer_3_out, multiplexer_4_out, PC, register_file_1_hi_2, register_file_1_lo_2, RND_t;
  wire [31:7] A;

  Random #(.width(32)) Random (.clk(Clock), .out(RND_t));  // open: next, clr
  Multiplexer #(.select(2), .width(32), .enable("false")) multiplexer_1 (
    .in0(PC), .in1(F), .in2({A, TTY_DATA}), .out(multiplexer_1_out), .sel(Memory_Selector));  // open: in3
  Register #(.width(32)) u_PC (.D(branch_control_1_out_9), .en(Enabled_PC), .Q(PC), .clk(Clock), .clr(or_1_out));
  or or_1 (or_1_out, Reset, halt);
  RAM_Manager ram_manager_1 (
    .Address_2(Addr), .Address(multiplexer_1_out), .RAM_In_0(Out_RAM0), .RAM_Out_0(In_RAM0),
    .RAM_In_1(Out_RAM1), .RAM_Out_1(In_RAM1), .RAM_In_2(Out_RAM2), .RAM_Out_2(In_RAM2), .RAM_In_3(Out_RAM3),
    .RAM_Out_3(In_RAM3), .Read_Time(RT), .Write_Time(WT), .Mask(Mask), .Out_Value(mem), .Selector_RT(SRT),
    .Selector_WT(SWT), .Clock(Clock), .RT__0(RT__0), .WT__0(WT__0), .Rt(B), .sw(or_2_out));
  or or_2 (or_2_out, sw, push);
  Multiplexer #(.select(3), .enable("false")) multiplexer_2 (
    .in0(1'b0), .in1(A_B_t), .in2(or_4_out), .in3(or_3_out), .in4(A_B_t_t), .in5(A_B),
    .out(multiplexer_2_out), .sel(Branch_Control_Selector));  // open: in6, in7
  Branch_Control branch_control_1 (
    .Current_Address_Instruction(PC), .K(K), .Current_Inst(mem), .Jump_Register({A, TTY_DATA}), .jmp(jmp),
    .FC(multiplexer_2_out), .JMP_Inst(j), .JR_Inst(jr), .out_9(branch_control_1_out_9));
  assign KBD_t = {{25{1'b0}}, KBD_DATA};  // Bit_Extender bit_extender_1
  or or_3 (or_3_out, A_B_t, A_B);
  or or_4 (or_4_out, A_B, A_B_t_t);
  and and_1 (RW, PreRW, CURW);
  Comparator #(.width(32), .mode("unsigned")) comparator_1 (
    .a(PC), .b({32{1'b0}}), .eq(First_Instruction));  // open: gt, lt
  D_Flip_Flop d_ff_1 (.clk(Clock), .D(halt), .Q(Stop), .reset(Reset));  // open: Qn, preset, en
  Register_File register_file_1 (
    .Clock(Clock), .DI(multiplexer_3_out), .Hi(Hi), .Lo(Lo), .A({A, TTY_DATA}), .B(B),
    .Hi_2(register_file_1_hi_2), .Lo_2(register_file_1_lo_2), .DA(DA), .RW(RW), .Reset(Reset),
    .Selector_A(SA), .Selector_B(SB), .EnabledHL(ENHL), .SP_0(out_24),
    .Stack_Point_Selector(Stack_Point_Selector));
  Multiplexer #(.select(3), .width(32), .enable("false")) multiplexer_3 (
    .in0(register_file_1_lo_2), .in1(register_file_1_hi_2), .in2(F), .in3(mem), .in4(KBD_t),
    .in5({32{1'b1}}), .in6(RND_t), .out(multiplexer_3_out), .sel(Selector_Data_Input));  // open: in7
  Multiplexer #(.width(32), .enable("false")) multiplexer_4 (.in0(B), .in1(K), .out(multiplexer_4_out), .sel(ALUSB));
  ALU alu_1 (
    .A({A, TTY_DATA}), .B(multiplexer_4_out), .OP(Op), .Hi(Hi), .Out(F), .Lo(Lo), .A_B(A_B_t_t),
    .A_B_2(A_B_t), .A_B_3(A_B));  // open: CF, ZF, SF
  ID id_1 (
    .Clock(Clock), .Instruction(Instruction_q), .K(K), .DA(DA), .SA(SA), .SB(SB), .Op(Op), .EnabledHL(ENHL),
    .RW(PreRW), .JMP(jmp), .nop(nop), .add(add), .sub(sub), .mul(mul), .mulu(mulu), .div(div), .divu(divu),
    .slt(slt), .sltu(sltu), .\and (\and ), .\or (\or ), .\nor (\nor ), .\xor (\xor ), .addi(addi),
    .slti(slti), .sltiu(sltiu), .andi(andi), .ori(ori), .xori(xori), .lw(lw), .sw(sw), .pop(pop),
    .push(push), .beq(beq), .bne(bne), .blez(blez), .bgtz(bgtz), .bltz(bltz), .j(j), .jr(jr), .mfhi(mfhi),
    .mflo(mflo), .halt(halt), .tty(tty), .kbd(kbd), .rnd(rnd));
  Register #(.width(32)) Instruction (.D(mem), .en(Enable_Instruction), .Q(Instruction_q), .clk(Clock), .clr(Reset));

  assign KBD_Clear = halt;
  assign TTY_Enable = tty;

  // Other names for the same wires on the sheet: A[6:0] = TTY_DATA; BCS[2:0] = Branch_Control_Selector; clk = Clock;
  //   En_Inst = Enable_Instruction; EN_PC = Enabled_PC; rst = Reset; SDI[2:0] = Selector_Data_Input

  // Notes on the sheet:
  //   Operaciones
endmodule

module ALU (
  input  [31:0] A,
  input  [31:0] B,
  input  [3:0] OP,
  output [31:0] Out,
  output A_B,
  output [31:0] Hi,
  output A_B_2,
  output A_B_3,
  output ZF,
  output SF,
  output [31:0] Lo,
  output CF
);

  wire addc, and_1_out, and_2_out, and_4_out, and_5_out, comparator_2_lt, comparator_3_lt, not_1_out,
       not_2_out, not_3_out, not_4_out, not_5_out, not_6_out, not_7_out, not_8_out, not_9_out, not_10_out,
       not_11_out, subc;
  wire [1:0] SC;
  wire [2:0] SLH;
  wire [31:0] add, \and , divHi, divLo, divuHi, divuLo, mulHi, mulLo, muluHi, muluLo, \nor , \or , stl, stlu,
       sub, \xor ;

  not not_1 (not_1_out, OP[2]);
  not not_2 (not_2_out, OP[1]);
  not not_3 (not_3_out, OP[3]);
  not not_4 (not_4_out, OP[1]);
  not not_5 (not_5_out, OP[3]);
  not not_6 (not_6_out, OP[2]);
  not not_7 (not_7_out, OP[3]);
  not not_8 (not_8_out, OP[1]);
  or or_1 (SC[1], OP[1], OP[2], OP[3]);
  not not_9 (not_9_out, OP[3]);
  not not_10 (not_10_out, OP[2]);
  not not_11 (not_11_out, OP[1]);
  Comparator #(.width(32)) comparator_1 (.a(A), .b(B), .gt(A_B), .eq(A_B_2), .lt(A_B_3));
  and and_1 (and_1_out, not_1_out, not_2_out);
  or or_2 (SLH[2], and_1_out, and_2_out, OP[3]);
  and and_2 (and_2_out, OP[2], OP[1]);
  and and_3 (SLH[1], not_3_out, OP[2], not_4_out);
  and and_4 (and_4_out, not_5_out, not_6_out, OP[1], OP[0]);
  or or_3 (SLH[0], and_4_out, and_5_out);
  and and_5 (and_5_out, not_7_out, OP[2], not_8_out, OP[0]);
  and and_6 (SC[0], not_9_out, not_10_out, not_11_out, OP[0]);
  assign \and  = A & B;  // AND_Gate and_7, 32 bits wide
  assign \nor  = ~(A | B);  // NOR_Gate nor_1, 32 bits wide
  Adder #(.width(32)) adder_1 (.a(A), .b(B), .out(add), .cout(addc));  // open: cin
  Multiplier #(.width(32)) multiplier_1 (.a(A), .b(B), .out(mulLo), .cout(mulHi));  // open: cin
  MULU mulu_1 (.A(A), .B(B), .Hi(muluHi), .Lo(muluLo));
  assign \or  = A | B;  // OR_Gate or_4, 32 bits wide
  assign \xor  = A ^ B;  // XOR_Gate xor_1, 32 bits wide
  S_DIV s_div_1 (.A(A), .B(B), .Lo(divLo), .Hi(divHi));
  Subtractor #(.width(32)) subtractor_1 (.a(A), .b(B), .out(sub), .bout(subc));  // open: bin
  Divider #(.width(32)) divider_1 (.a(A), .b(B), .out(divuLo), .rem(divuHi));  // open: upper
  Comparator #(.width(32)) comparator_2 (.a(A), .b(B), .lt(comparator_2_lt));  // open: gt, eq
  Comparator #(.width(32), .mode("unsigned")) comparator_3 (.a(A), .b(B), .lt(comparator_3_lt));  // open: gt, eq
  Multiplexer #(.width(32), .enable("false")) multiplexer_1 (
    .in0({32{1'b0}}), .in1(32'h1), .out(stl), .sel(comparator_2_lt));
  Multiplexer #(.width(32), .enable("false")) multiplexer_2 (
    .in0({32{1'b0}}), .in1(32'h1), .out(stlu), .sel(comparator_3_lt));
  Multiplexer #(.select(4), .width(32), .enable("false")) multiplexer_3 (
    .in0(add), .in1(sub), .in2({32{1'b0}}), .in3({32{1'b0}}), .in4({32{1'b0}}), .in5({32{1'b0}}), .in6(stl),
    .in7(stlu), .in8(\and ), .in9(\or ), .in10(\nor ), .in11(\xor ), .out(Out), .sel(OP));  // open: in12, in13, in14, in15
  Multiplexer #(.select(2), .enable("false")) multiplexer_4 (
    .in0(addc), .in1(subc), .in2(1'b0), .out(CF), .sel(SC));  // open: in3
  Multiplexer #(.select(3), .width(32), .enable("false")) multiplexer_5 (
    .in0(mulHi), .in1(muluHi), .in2(divHi), .in3(divuHi), .in4({32{1'b0}}), .out(Hi), .sel(SLH));  // open: in5, in6, in7
  Multiplexer #(.select(3), .width(32), .enable("false")) multiplexer_6 (
    .in0(mulLo), .in1(muluLo), .in2(divLo), .in3(divuLo), .in4({32{1'b0}}), .out(Lo), .sel(SLH));  // open: in5, in6, in7
  Comparator #(.width(32)) comparator_4 (.a(Out), .b({32{1'b0}}), .eq(ZF), .lt(SF));  // open: gt

  // Other names for the same wires on the sheet: op1 = OP[0]; op2 = OP[1]; op3 = OP[2]; op4 = OP[3]

  // Notes on the sheet:
  //   INPUT:
  //   Selectores
  //   Selector Lo and Hi
  //   Selector Carry
  //   Op lógicas
  //   add
  //   mul
  //   mulu
  //   Op aritméticas:
  //   sub
  //   div
  //   divu
  //   sltu
  //   slt
  //   OUTPUT:
endmodule

module Register_File (
  input  [31:0] DI,
  input  Clock,
  input  [1:0] Stack_Point_Selector,
  input  RW,
  input  [4:0] Selector_A,
  input  [4:0] Selector_B,
  input  EnabledHL,
  input  [31:0] Hi,
  input  [31:0] Lo,
  input  [4:0] DA,
  input  Reset,
  output [31:0] A,
  output [31:0] B,
  output SP_0,
  output [31:0] Hi_2,
  output [31:0] Lo_2
);

  wire demultiplexer_1_out0, demultiplexer_1_out1, demultiplexer_1_out2, demultiplexer_1_out3,
       demultiplexer_1_out4, demultiplexer_1_out5, demultiplexer_1_out6, demultiplexer_1_out7,
       demultiplexer_1_out8, demultiplexer_1_out9, demultiplexer_1_out10, demultiplexer_1_out11,
       demultiplexer_1_out12, demultiplexer_1_out13, demultiplexer_1_out14, demultiplexer_1_out15,
       demultiplexer_1_out16, demultiplexer_1_out17, demultiplexer_1_out18, demultiplexer_1_out19,
       demultiplexer_1_out20, demultiplexer_1_out21, demultiplexer_1_out22, demultiplexer_1_out23,
       demultiplexer_1_out24, demultiplexer_1_out25, demultiplexer_1_out26, demultiplexer_1_out27,
       demultiplexer_1_out28, demultiplexer_1_out29, demultiplexer_1_out30, en32;
  wire [31:0] multiplexer_3_out, multiplexer_4_out, Pop, Push, Q1, Q2, Q3, Q4, Q5, Q6, Q7, Q8, Q9, Q10, Q11,
       Q12, Q13, Q14, Q15, Q16, Q17, Q18, Q19, Q20, Q21, Q22, Q23, Q24, Q25, Q26, Q27, Q28, Q29, Q30, Q31,
       Q32;

  Demultiplexer #(.select(5), .enable("false")) demultiplexer_1 (
    .out0(demultiplexer_1_out0), .out1(demultiplexer_1_out1), .out2(demultiplexer_1_out2),
    .out3(demultiplexer_1_out3), .out4(demultiplexer_1_out4), .out5(demultiplexer_1_out5),
    .out6(demultiplexer_1_out6), .out7(demultiplexer_1_out7), .out8(demultiplexer_1_out8),
    .out9(demultiplexer_1_out9), .out10(demultiplexer_1_out10), .out11(demultiplexer_1_out11),
    .out12(demultiplexer_1_out12), .out13(demultiplexer_1_out13), .out14(demultiplexer_1_out14),
    .out15(demultiplexer_1_out15), .out16(demultiplexer_1_out16), .out17(demultiplexer_1_out17),
    .out18(demultiplexer_1_out18), .out19(demultiplexer_1_out19), .out20(demultiplexer_1_out20),
    .out21(demultiplexer_1_out21), .out22(demultiplexer_1_out22), .out23(demultiplexer_1_out23),
    .out24(demultiplexer_1_out24), .out25(demultiplexer_1_out25), .out26(demultiplexer_1_out26),
    .out27(demultiplexer_1_out27), .out28(demultiplexer_1_out28), .out29(demultiplexer_1_out29),
    .out30(demultiplexer_1_out30), .out31(en32), .in(RW), .sel(DA));
  _32_Registers_of_32_bits u_32_registers_of_32_bits_1 (
    .in_1(demultiplexer_1_out0), .A(DI), .in_3(demultiplexer_1_out1), .Clock(Clock), .Reset(Reset),
    .in_6(demultiplexer_1_out2), .in_7(demultiplexer_1_out3), .in_8(demultiplexer_1_out4),
    .in_9(demultiplexer_1_out5), .in_10(demultiplexer_1_out6), .in_11(demultiplexer_1_out7),
    .in_12(demultiplexer_1_out8), .in_13(demultiplexer_1_out9), .in_14(demultiplexer_1_out10),
    .in_15(demultiplexer_1_out11), .in_16(demultiplexer_1_out12), .in_17(demultiplexer_1_out13),
    .in_18(demultiplexer_1_out14), .in_19(demultiplexer_1_out15), .in_20(demultiplexer_1_out16),
    .in_21(demultiplexer_1_out17), .in_22(demultiplexer_1_out18), .in_23(demultiplexer_1_out19),
    .in_24(demultiplexer_1_out20), .in_25(demultiplexer_1_out21), .in_26(demultiplexer_1_out22),
    .in_27(demultiplexer_1_out23), .in_28(demultiplexer_1_out24), .in_29(demultiplexer_1_out25),
    .in_30(demultiplexer_1_out26), .in_31(demultiplexer_1_out27), .in_32(demultiplexer_1_out28),
    .in_33(demultiplexer_1_out29), .in_34(demultiplexer_1_out30), .out_35(Q1), .out_36(Q2), .out_37(Q3),
    .out_38(Q4), .out_39(Q5), .out_40(Q6), .out_41(Q7), .out_42(Q8), .out_43(Q9), .out_44(Q10), .out_45(Q11),
    .out_46(Q12), .out_47(Q13), .out_48(Q14), .out_49(Q15), .out_50(Q16), .out_51(Q17), .out_52(Q18),
    .out_53(Q19), .out_54(Q20), .out_55(Q21), .out_56(Q22), .out_57(Q23), .out_58(Q24), .out_59(Q25),
    .out_60(Q26), .out_61(Q27), .out_62(Q28), .out_63(Q29), .out_64(Q30), .out_65(Q31));
  Multiplexer #(.select(5), .width(32), .enable("false")) multiplexer_1 (
    .in0(Q1), .in1(Q2), .in2(Q3), .in3(Q4), .in4(Q5), .in5(Q6), .in6(Q7), .in7(Q8), .in8(Q9), .in9(Q10),
    .in10(Q11), .in11(Q12), .in12(Q13), .in13(Q14), .in14(Q15), .in15(Q16), .in16(Q17), .in17(Q18),
    .in18(Q19), .in19(Q20), .in20(Q21), .in21(Q22), .in22(Q23), .in23(Q24), .in24(Q25), .in25(Q26),
    .in26(Q27), .in27(Q28), .in28(Q29), .in29(Q30), .in30(Q31), .in31(Q32), .out(A), .sel(Selector_A));
  Multiplexer #(.select(5), .width(32), .enable("false")) multiplexer_2 (
    .in0(Q1), .in1(Q2), .in2(Q3), .in3(Q4), .in4(Q5), .in5(Q6), .in6(Q7), .in7(Q8), .in8(Q9), .in9(Q10),
    .in10(Q11), .in11(Q12), .in12(Q13), .in13(Q14), .in14(Q15), .in15(Q16), .in16(Q17), .in17(Q18),
    .in18(Q19), .in19(Q20), .in20(Q21), .in21(Q22), .in22(Q23), .in23(Q24), .in24(Q25), .in25(Q26),
    .in26(Q27), .in27(Q28), .in28(Q29), .in29(Q30), .in30(Q31), .in31(Q32), .out(B), .sel(Selector_B));
  Multiplexer #(.select(2), .width(32), .enable("false")) multiplexer_3 (
    .in0(Q32), .in1({32{1'b0}}), .in2(Pop), .in3(Push), .out(multiplexer_3_out), .sel(Stack_Point_Selector));
  Register #(.width(32)) register_1 (.D(Hi), .en(EnabledHL), .Q(Hi_2), .clk(Clock), .clr(Reset));
  Multiplexer #(.width(32)) multiplexer_4 (
    .in0(multiplexer_3_out), .in1(DI), .out(multiplexer_4_out), .sel(en32));  // open: en
  Register #(.width(32)) ESP (.D(multiplexer_4_out), .Q(Q32), .clk(Clock), .clr(Reset));  // open: en
  Adder #(.width(32)) adder_1 (.a(Q32), .b(32'h4), .out(Pop));  // open: cin, cout
  Subtractor #(.width(32)) subtractor_1 (.a(Q32), .b(32'h4), .out(Push));  // open: bin, bout
  Comparator #(.width(32)) comparator_1 (.a(Q32), .b({32{1'b0}}), .eq(SP_0));  // open: gt, lt
  Register #(.width(32)) register_2 (.D(Lo), .en(EnabledHL), .Q(Lo_2), .clk(Clock), .clr(Reset));

  // Other names for the same wires on the sheet: CLK = Clock; ehl = EnabledHL; SP[31:0] = Q32

  // Notes on the sheet:
  //   INPUT:
  //   OUTPUT:
  //   Stack Pointer
  //   Hi-Lo
endmodule

module ID (
  input  Clock,
  input  [31:0] Instruction,
  output [4:0] DA,
  output [31:0] K,
  output EnabledHL,
  output \and ,
  output bltz,
  output nop,
  output xori,
  output RW,
  output \or ,
  output j,
  output add,
  output lw,
  output [4:0] SA,
  output JMP,
  output \nor ,
  output jr,
  output sub,
  output sw,
  output [4:0] SB,
  output \xor ,
  output mfhi,
  output mul,
  output pop,
  output [3:0] Op,
  output addi,
  output mflo,
  output mulu,
  output push,
  output slti,
  output halt,
  output div,
  output beq,
  output sltiu,
  output tty,
  output divu,
  output bne,
  output andi,
  output rnd,
  output slt,
  output blez,
  output ori,
  output kbd,
  output sltu,
  output bgtz
);

  wire add_t, and_1_out, and_2_out, and_t, minus_RW, nor_1_out, not_1_out, not_2_out, not_3_out, not_4_out,
       not_5_out, not_6_out, not_7_out, not_8_out, not_9_out, not_10_out, not_11_out, not_12_out, not_13_out,
       not_14_out, not_15_out, not_16_out, not_17_out, not_18_out, not_19_out, not_20_out, not_21_out,
       not_22_out, not_23_out, not_24_out, not_25_out, not_26_out, not_27_out, not_28_out, not_29_out,
       not_30_out, not_31_out, not_32_out, not_33_out, not_34_out, not_35_out, not_36_out, not_37_out,
       not_38_out, not_39_out, not_40_out, not_41_out, not_42_out, not_43_out, not_44_out, not_45_out,
       not_46_out, not_47_out, not_48_out, not_49_out, not_50_out, not_51_out, not_52_out, not_53_out,
       not_54_out, not_55_out, not_56_out, not_57_out, not_58_out, not_59_out, not_60_out, not_61_out,
       not_62_out, not_63_out, not_64_out, not_65_out, not_66_out, not_67_out, not_68_out, not_69_out,
       not_70_out, not_71_out, not_72_out, not_73_out, not_74_out, not_75_out, not_76_out, not_77_out,
       not_78_out, not_79_out, not_80_out, not_81_out, not_82_out, not_83_out, not_84_out, not_85_out,
       not_86_out, not_87_out, not_88_out, not_89_out, not_90_out, not_91_out, not_92_out, not_93_out,
       not_94_out, not_95_out, not_96_out, not_97_out, not_98_out, not_99_out, not_100_out, not_101_out,
       not_102_out, not_103_out, not_104_out, not_105_out, not_106_out, not_107_out, not_108_out,
       not_109_out, not_110_out, not_111_out, not_112_out, not_113_out, not_114_out, not_115_out,
       not_116_out, not_117_out, not_118_out, not_119_out, not_120_out, not_121_out, not_122_out,
       not_123_out, not_124_out, not_125_out, not_126_out, not_127_out, not_128_out, not_129_out,
       not_130_out, not_131_out, not_132_out, not_133_out, not_134_out, not_135_out, not_136_out,
       not_137_out, not_138_out, not_139_out, not_140_out, not_141_out, not_142_out, not_143_out,
       not_144_out, not_145_out, not_146_out, not_147_out, not_148_out, not_149_out, not_150_out,
       not_151_out, not_152_out, not_153_out, not_154_out, not_155_out, not_156_out, not_157_out,
       not_158_out, not_159_out, not_160_out, not_161_out, not_162_out, not_163_out, not_164_out,
       not_165_out, not_166_out, not_167_out, not_168_out, not_169_out, not_170_out, not_171_out,
       not_172_out, not_173_out, not_174_out, not_175_out, not_176_out, not_177_out, not_178_out,
       not_179_out, not_180_out, not_181_out, not_182_out, not_183_out, not_184_out, not_185_out,
       not_186_out, not_187_out, not_188_out, not_189_out, not_190_out, not_191_out, not_192_out,
       not_193_out, not_194_out, not_195_out, not_196_out, not_197_out, not_198_out, not_199_out,
       not_200_out, not_201_out, not_202_out, not_203_out, not_204_out, not_205_out, not_206_out,
       not_207_out, not_208_out, not_209_out, not_210_out, not_211_out, not_212_out, not_213_out,
       not_214_out, not_215_out, not_216_out, not_217_out, not_218_out, not_219_out, not_220_out,
       not_221_out, not_222_out, not_223_out, not_224_out, not_225_out, not_226_out, not_227_out,
       not_228_out, not_229_out, not_230_out, not_231_out, not_232_out, not_233_out, not_234_out,
       not_235_out, not_236_out, not_237_out, not_238_out, not_239_out, not_240_out, not_241_out, or_1_out,
       or_2_out, or_4_out, or_5_out, or_8_out, or_9_out, or_12_out, or_13_out, or_t, priority_encoder_1_gs,
       sa_t, slt_t, sltu_t, so, sub_t, xor_t;
  wire [1:0] priority_encoder_2_out, priority_encoder_3_out;
  wire [3:0] choose_operation_1_op0, register_1_q;
  wire [31:0] adder_1_out, bit_extender_1_out, bit_extender_2_out, multiplier_1_out;

  Choose_Operation choose_operation_1 (
    .add(add_t), .sub(sub_t), .mul(mul), .mulu(mulu), .div(div), .divu(divu), .slt(slt_t), .sltu(sltu_t),
    .\and (and_t), .\or (or_t), .\nor (\nor ), .\xor (xor_t), .op3(choose_operation_1_op0[3]),
    .op2(choose_operation_1_op0[2]), .op1(choose_operation_1_op0[1]), .op0(choose_operation_1_op0[0]));
  or or_1 (or_1_out, add, sub, slt, sltu, \and , \or , \nor , \xor , pop, mfhi, mflo, rnd, kbd);
  and and_1 (and_1_out, or_1_out, or_2_out);
  nor nor_1 (nor_1_out, or_1_out, or_2_out);
  not not_1 (not_1_out, or_1_out);
  or or_2 (or_2_out, addi, slti, andi, ori, xori);
  or or_3 (sa_t, add, sub, mul, mulu, div, divu, slt, sltu, \and , \or , \nor , \xor , push, mfhi, mflo, beq, bne);
  not not_2 (not_2_out, Instruction[0]);
  not not_3 (not_3_out, Instruction[1]);
  not not_4 (not_4_out, Instruction[2]);
  not not_5 (not_5_out, Instruction[3]);
  not not_6 (not_6_out, Instruction[4]);
  not not_7 (not_7_out, Instruction[26]);
  not not_8 (not_8_out, Instruction[27]);
  not not_9 (not_9_out, Instruction[28]);
  not not_10 (not_10_out, Instruction[29]);
  not not_11 (not_11_out, Instruction[30]);
  not not_12 (not_12_out, Instruction[31]);
  not not_13 (not_13_out, Instruction[26]);
  not not_14 (not_14_out, Instruction[27]);
  not not_15 (not_15_out, Instruction[28]);
  not not_16 (not_16_out, Instruction[30]);
  not not_17 (not_17_out, Instruction[31]);
  not not_18 (not_18_out, Instruction[28]);
  not not_19 (not_19_out, Instruction[29]);
  not not_20 (not_20_out, Instruction[30]);
  not not_21 (not_21_out, Instruction[28]);
  not not_22 (not_22_out, Instruction[30]);
  not not_23 (not_23_out, Instruction[0]);
  not not_24 (not_24_out, Instruction[1]);
  not not_25 (not_25_out, Instruction[2]);
  not not_26 (not_26_out, Instruction[3]);
  not not_27 (not_27_out, Instruction[4]);
  not not_28 (not_28_out, Instruction[5]);
  not not_29 (not_29_out, Instruction[26]);
  not not_30 (not_30_out, Instruction[27]);
  not not_31 (not_31_out, Instruction[28]);
  not not_32 (not_32_out, Instruction[0]);
  not not_33 (not_33_out, Instruction[2]);
  not not_34 (not_34_out, Instruction[3]);
  not not_35 (not_35_out, Instruction[4]);
  not not_36 (not_36_out, Instruction[26]);
  not not_37 (not_37_out, Instruction[27]);
  not not_38 (not_38_out, Instruction[28]);
  not not_39 (not_39_out, Instruction[29]);
  not not_40 (not_40_out, Instruction[30]);
  not not_41 (not_41_out, Instruction[31]);
  not not_42 (not_42_out, Instruction[1]);
  not not_43 (not_43_out, Instruction[2]);
  not not_44 (not_44_out, Instruction[3]);
  not not_45 (not_45_out, Instruction[4]);
  not not_46 (not_46_out, Instruction[5]);
  not not_47 (not_47_out, Instruction[26]);
  not not_48 (not_48_out, Instruction[27]);
  not not_49 (not_49_out, Instruction[28]);
  not not_50 (not_50_out, Instruction[0]);
  not not_51 (not_51_out, Instruction[1]);
  not not_52 (not_52_out, Instruction[2]);
  not not_53 (not_53_out, Instruction[5]);
  not not_54 (not_54_out, Instruction[26]);
  not not_55 (not_55_out, Instruction[27]);
  not not_56 (not_56_out, Instruction[28]);
  not not_57 (not_57_out, Instruction[29]);
  not not_58 (not_58_out, Instruction[30]);
  not not_59 (not_59_out, Instruction[31]);
  not not_60 (not_60_out, Instruction[26]);
  not not_61 (not_61_out, Instruction[27]);
  not not_62 (not_62_out, Instruction[29]);
  not not_63 (not_63_out, Instruction[30]);
  not not_64 (not_64_out, Instruction[31]);
  not not_65 (not_65_out, Instruction[27]);
  not not_66 (not_66_out, Instruction[29]);
  not not_67 (not_67_out, Instruction[30]);
  not not_68 (not_68_out, Instruction[31]);
  not not_69 (not_69_out, Instruction[26]);
  not not_70 (not_70_out, Instruction[29]);
  not not_71 (not_71_out, Instruction[30]);
  not not_72 (not_72_out, Instruction[31]);
  Comparator #(.width(4)) comparator_1 (.a(choose_operation_1_op0), .b(4'b1100), .eq(so));  // open: gt, lt
  Multiplexer #(.width(4), .enable("false")) multiplexer_1 (
    .in0(choose_operation_1_op0), .in1(register_1_q), .out(Op), .sel(so));
  Register #(.width(4)) register_1 (.D(Op), .Q(register_1_q), .clk(Clock));  // open: en, clr
  or or_4 (or_4_out, and_1_out, nor_1_out);
  Priority_Encoder #(.select(1)) priority_encoder_1 (
    .in0(or_4_out), .in1(and_2_out), .gs(priority_encoder_1_gs));  // open: out, en_out, en_in
  and and_2 (and_2_out, not_1_out, or_2_out);
  and and_3 (add, not_2_out, not_3_out, not_4_out, not_5_out, not_6_out, Instruction[5], not_7_out, not_8_out, not_9_out, not_10_out, not_11_out, not_12_out);
  and and_4 (addi, not_13_out, not_14_out, not_15_out, Instruction[29], not_16_out, not_17_out);
  and and_5 (lw, Instruction[26], Instruction[27], not_18_out, not_19_out, not_20_out, Instruction[31]);
  and and_6 (sw, Instruction[26], Instruction[27], not_21_out, Instruction[29], not_22_out, Instruction[31]);
  and and_7 (pop, not_23_out, not_24_out, not_25_out, not_26_out, not_27_out, not_28_out, not_29_out, not_30_out, not_31_out, Instruction[29], Instruction[30], Instruction[31]);
  and and_8 (sub, not_32_out, Instruction[1], not_33_out, not_34_out, not_35_out, Instruction[5], not_36_out, not_37_out, not_38_out, not_39_out, not_40_out, not_41_out);
  and and_9 (push, Instruction[0], not_42_out, not_43_out, not_44_out, not_45_out, not_46_out, not_47_out, not_48_out, not_49_out, Instruction[29], Instruction[30], Instruction[31]);
  and and_10 (mul, not_50_out, not_51_out, not_52_out, Instruction[3], Instruction[4], not_53_out, not_54_out, not_55_out, not_56_out, not_57_out, not_58_out, not_59_out);
  and and_11 (beq, not_60_out, not_61_out, Instruction[28], not_62_out, not_63_out, not_64_out);
  and and_12 (bne, Instruction[26], not_65_out, Instruction[28], not_66_out, not_67_out, not_68_out);
  and and_13 (blez, not_69_out, Instruction[27], Instruction[28], not_70_out, not_71_out, not_72_out);
  Multiplexer #(.width(5), .enable("false")) multiplexer_2 (
    .in0(Instruction[15:11]), .in1(Instruction[20:16]), .out(DA), .sel(priority_encoder_1_gs));
  Multiplexer #(.width(5), .enable("false")) multiplexer_3 (
    .in0(Instruction[25:21]), .in1({5{1'b1}}), .out(SA), .sel(or_5_out));
  or or_5 (or_5_out, push, pop);
  or or_6 (add_t, add, addi, lw, sw, pop);
  or or_7 (sub_t, sub, push);
  not not_73 (not_73_out, Instruction[29]);
  not not_74 (not_74_out, Instruction[30]);
  not not_75 (not_75_out, Instruction[31]);
  not not_76 (not_76_out, Instruction[27]);
  not not_77 (not_77_out, Instruction[28]);
  not not_78 (not_78_out, Instruction[29]);
  not not_79 (not_79_out, Instruction[30]);
  not not_80 (not_80_out, Instruction[31]);
  not not_81 (not_81_out, Instruction[1]);
  not not_82 (not_82_out, Instruction[2]);
  not not_83 (not_83_out, Instruction[5]);
  not not_84 (not_84_out, Instruction[26]);
  not not_85 (not_85_out, Instruction[27]);
  not not_86 (not_86_out, Instruction[28]);
  not not_87 (not_87_out, Instruction[29]);
  not not_88 (not_88_out, Instruction[30]);
  not not_89 (not_89_out, Instruction[31]);
  not not_90 (not_90_out, Instruction[0]);
  not not_91 (not_91_out, Instruction[2]);
  not not_92 (not_92_out, Instruction[5]);
  not not_93 (not_93_out, Instruction[26]);
  not not_94 (not_94_out, Instruction[27]);
  not not_95 (not_95_out, Instruction[28]);
  not not_96 (not_96_out, Instruction[29]);
  not not_97 (not_97_out, Instruction[30]);
  not not_98 (not_98_out, Instruction[31]);
  not not_99 (not_99_out, Instruction[2]);
  not not_100 (not_100_out, Instruction[5]);
  not not_101 (not_101_out, Instruction[26]);
  not not_102 (not_102_out, Instruction[27]);
  not not_103 (not_103_out, Instruction[28]);
  not not_104 (not_104_out, Instruction[29]);
  not not_105 (not_105_out, Instruction[30]);
  not not_106 (not_106_out, Instruction[31]);
  not not_107 (not_107_out, Instruction[0]);
  not not_108 (not_108_out, Instruction[2]);
  not not_109 (not_109_out, Instruction[4]);
  not not_110 (not_110_out, Instruction[26]);
  not not_111 (not_111_out, Instruction[27]);
  not not_112 (not_112_out, Instruction[28]);
  not not_113 (not_113_out, Instruction[29]);
  not not_114 (not_114_out, Instruction[30]);
  not not_115 (not_115_out, Instruction[31]);
  not not_116 (not_116_out, Instruction[26]);
  not not_117 (not_117_out, Instruction[28]);
  not not_118 (not_118_out, Instruction[30]);
  not not_119 (not_119_out, Instruction[31]);
  not not_120 (not_120_out, Instruction[2]);
  not not_121 (not_121_out, Instruction[4]);
  not not_122 (not_122_out, Instruction[26]);
  not not_123 (not_123_out, Instruction[27]);
  not not_124 (not_124_out, Instruction[28]);
  not not_125 (not_125_out, Instruction[29]);
  not not_126 (not_126_out, Instruction[30]);
  not not_127 (not_127_out, Instruction[31]);
  not not_128 (not_128_out, Instruction[28]);
  not not_129 (not_129_out, Instruction[30]);
  not not_130 (not_130_out, Instruction[31]);
  and and_14 (bgtz, Instruction[26], Instruction[27], Instruction[28], not_73_out, not_74_out, not_75_out);
  and and_15 (bltz, Instruction[26], not_76_out, not_77_out, not_78_out, not_79_out, not_80_out);
  not not_131 (not_131_out, Instruction[0]);
  not not_132 (not_132_out, Instruction[1]);
  not not_133 (not_133_out, Instruction[2]);
  not not_134 (not_134_out, Instruction[4]);
  not not_135 (not_135_out, Instruction[5]);
  and and_16 (jr, not_131_out, not_132_out, not_133_out, Instruction[3], not_134_out, not_135_out, not_136_out, not_137_out, not_138_out, not_139_out, not_140_out, not_141_out);
  not not_136 (not_136_out, Instruction[26]);
  not not_137 (not_137_out, Instruction[27]);
  not not_138 (not_138_out, Instruction[28]);
  not not_139 (not_139_out, Instruction[29]);
  not not_140 (not_140_out, Instruction[30]);
  not not_141 (not_141_out, Instruction[31]);
  or or_8 (or_8_out, sw, add, sub, mul, mulu, div, divu, slt, sltu, \and , \or , \nor , \xor , mfhi, beq, bne);
  or or_9 (or_9_out, blez, bgtz, bltz, jr, j);
  and and_17 (mulu, Instruction[0], not_81_out, not_82_out, Instruction[3], Instruction[4], not_83_out, not_84_out, not_85_out, not_86_out, not_87_out, not_88_out, not_89_out);
  and and_18 (div, not_90_out, Instruction[1], not_91_out, Instruction[3], Instruction[4], not_92_out, not_93_out, not_94_out, not_95_out, not_96_out, not_97_out, not_98_out);
  and and_19 (divu, Instruction[0], Instruction[1], not_99_out, Instruction[3], Instruction[4], not_100_out, not_101_out, not_102_out, not_103_out, not_104_out, not_105_out, not_106_out);
  and and_20 (slt, not_107_out, Instruction[1], not_108_out, Instruction[3], not_109_out, Instruction[5], not_110_out, not_111_out, not_112_out, not_113_out, not_114_out, not_115_out);
  or or_10 (slt_t, slt, slti);
  and and_21 (slti, not_116_out, Instruction[27], not_117_out, Instruction[29], not_118_out, not_119_out);
  and and_22 (sltu, Instruction[0], Instruction[1], not_120_out, Instruction[3], not_121_out, Instruction[5], not_122_out, not_123_out, not_124_out, not_125_out, not_126_out, not_127_out);
  or or_11 (sltu_t, sltu, sltiu);
  and and_23 (sltiu, Instruction[26], Instruction[27], not_128_out, Instruction[29], not_129_out, not_130_out);
  or or_12 (or_12_out, addi, slti, sltiu, andi, ori, xori, lw, sw);
  Priority_Encoder #(.select(2)) priority_encoder_2 (
    .in1(1'b1), .in2(or_12_out), .in3(or_13_out), .out(priority_encoder_2_out));  // open: in0, gs, en_out, en_in
  or or_13 (or_13_out, beq, bne, blez, bgtz, bltz);
  Priority_Encoder #(.select(2)) priority_encoder_3 (
    .in0(1'b1), .in1(or_8_out), .in2(or_9_out), .in3(push), .out(priority_encoder_3_out));  // open: gs, en_out, en_in
  not not_142 (not_142_out, Instruction[26]);
  not not_143 (not_143_out, Instruction[28]);
  not not_144 (not_144_out, Instruction[29]);
  not not_145 (not_145_out, Instruction[30]);
  not not_146 (not_146_out, Instruction[31]);
  not not_147 (not_147_out, Instruction[26]);
  not not_148 (not_148_out, Instruction[27]);
  not not_149 (not_149_out, Instruction[30]);
  not not_150 (not_150_out, Instruction[31]);
  not not_151 (not_151_out, Instruction[27]);
  not not_152 (not_152_out, Instruction[30]);
  not not_153 (not_153_out, Instruction[31]);
  not not_154 (not_154_out, Instruction[26]);
  not not_155 (not_155_out, Instruction[30]);
  not not_156 (not_156_out, Instruction[31]);
  not not_157 (not_157_out, Instruction[0]);
  not not_158 (not_158_out, Instruction[1]);
  not not_159 (not_159_out, Instruction[2]);
  not not_160 (not_160_out, Instruction[3]);
  not not_161 (not_161_out, Instruction[4]);
  not not_162 (not_162_out, Instruction[5]);
  not not_163 (not_163_out, Instruction[26]);
  not not_164 (not_164_out, Instruction[27]);
  not not_165 (not_165_out, Instruction[28]);
  not not_166 (not_166_out, Instruction[29]);
  not not_167 (not_167_out, Instruction[30]);
  not not_168 (not_168_out, Instruction[31]);
  and and_24 (j, not_142_out, Instruction[27], not_143_out, not_144_out, not_145_out, not_146_out);
  assign bit_extender_1_out = {{16{Instruction[15]}}, Instruction[15:0]};  // Bit_Extender bit_extender_1
  assign bit_extender_2_out = {{16{Instruction[15]}}, Instruction[15:0]};  // Bit_Extender bit_extender_2
  Multiplexer #(.select(2), .width(5), .enable("false")) multiplexer_4 (
    .in0({5{1'b0}}), .in1(Instruction[20:16]), .in2({5{1'b0}}), .in3(Instruction[25:21]), .out(SB),
    .sel(priority_encoder_3_out));
  not not_169 (not_169_out, Instruction[0]);
  not not_170 (not_170_out, Instruction[1]);
  not not_171 (not_171_out, Instruction[3]);
  not not_172 (not_172_out, Instruction[4]);
  and and_25 (\and , not_169_out, not_170_out, Instruction[2], not_171_out, not_172_out, Instruction[5], not_173_out, not_174_out, not_175_out, not_176_out, not_177_out, not_178_out);
  not not_173 (not_173_out, Instruction[26]);
  not not_174 (not_174_out, Instruction[27]);
  not not_175 (not_175_out, Instruction[28]);
  not not_176 (not_176_out, Instruction[29]);
  not not_177 (not_177_out, Instruction[30]);
  not not_178 (not_178_out, Instruction[31]);
  and and_26 (andi, not_147_out, not_148_out, Instruction[28], Instruction[29], not_149_out, not_150_out);
  not not_179 (not_179_out, Instruction[1]);
  not not_180 (not_180_out, Instruction[3]);
  not not_181 (not_181_out, Instruction[4]);
  and and_27 (\or , Instruction[0], not_179_out, Instruction[2], not_180_out, not_181_out, Instruction[5], not_182_out, not_183_out, not_184_out, not_185_out, not_186_out, not_187_out);
  not not_182 (not_182_out, Instruction[26]);
  not not_183 (not_183_out, Instruction[27]);
  not not_184 (not_184_out, Instruction[28]);
  not not_185 (not_185_out, Instruction[29]);
  not not_186 (not_186_out, Instruction[30]);
  not not_187 (not_187_out, Instruction[31]);
  and and_28 (ori, Instruction[26], not_151_out, Instruction[28], Instruction[29], not_152_out, not_153_out);
  not not_188 (not_188_out, Instruction[3]);
  not not_189 (not_189_out, Instruction[4]);
  and and_29 (\nor , Instruction[0], Instruction[1], Instruction[2], not_188_out, not_189_out, Instruction[5], not_190_out, not_191_out, not_192_out, not_193_out, not_194_out, not_195_out);
  not not_190 (not_190_out, Instruction[26]);
  not not_191 (not_191_out, Instruction[27]);
  not not_192 (not_192_out, Instruction[28]);
  not not_193 (not_193_out, Instruction[29]);
  not not_194 (not_194_out, Instruction[30]);
  not not_195 (not_195_out, Instruction[31]);
  not not_196 (not_196_out, Instruction[0]);
  not not_197 (not_197_out, Instruction[1]);
  not not_198 (not_198_out, Instruction[2]);
  not not_199 (not_199_out, Instruction[4]);
  and and_30 (\xor , not_196_out, not_197_out, not_198_out, Instruction[3], not_199_out, Instruction[5], not_200_out, not_201_out, not_202_out, not_203_out, not_204_out, not_205_out);
  not not_200 (not_200_out, Instruction[26]);
  not not_201 (not_201_out, Instruction[27]);
  not not_202 (not_202_out, Instruction[28]);
  not not_203 (not_203_out, Instruction[29]);
  not not_204 (not_204_out, Instruction[30]);
  not not_205 (not_205_out, Instruction[31]);
  and and_31 (xori, not_154_out, Instruction[27], Instruction[28], Instruction[29], not_155_out, not_156_out);
  and and_32 (nop, not_157_out, not_158_out, not_159_out, not_160_out, not_161_out, not_162_out, not_163_out, not_164_out, not_165_out, not_166_out, not_167_out, not_168_out);
  or or_14 (and_t, \and , andi);
  or or_15 (or_t, \or , ori);
  or or_16 (xor_t, \xor , xori);
  Adder #(.width(32)) adder_1 (.a(32'h4), .b(multiplier_1_out), .out(adder_1_out));  // open: cin, cout
  Multiplier #(.width(32)) multiplier_1 (.a(bit_extender_2_out), .b(32'h4), .out(multiplier_1_out));  // open: cin, cout
  or or_17 (JMP, beq, bne, blez, bgtz, bltz, jr, j);
  Multiplexer #(.select(2), .width(32), .enable("false")) multiplexer_5 (
    .in1({32{1'b0}}), .in2(bit_extender_1_out), .in3(adder_1_out), .out(K), .sel(priority_encoder_2_out));  // open: in0
  not not_206 (not_206_out, Instruction[0]);
  not not_207 (not_207_out, Instruction[1]);
  not not_208 (not_208_out, Instruction[2]);
  not not_209 (not_209_out, Instruction[3]);
  not not_210 (not_210_out, Instruction[5]);
  and and_33 (mfhi, not_206_out, not_207_out, not_208_out, not_209_out, Instruction[4], not_210_out, not_211_out, not_212_out, not_213_out, not_214_out, not_215_out, not_216_out);
  not not_211 (not_211_out, Instruction[26]);
  not not_212 (not_212_out, Instruction[27]);
  not not_213 (not_213_out, Instruction[28]);
  not not_214 (not_214_out, Instruction[29]);
  not not_215 (not_215_out, Instruction[30]);
  not not_216 (not_216_out, Instruction[31]);
  not not_217 (not_217_out, Instruction[0]);
  not not_218 (not_218_out, Instruction[2]);
  not not_219 (not_219_out, Instruction[3]);
  not not_220 (not_220_out, Instruction[5]);
  and and_34 (mflo, not_217_out, Instruction[1], not_218_out, not_219_out, Instruction[4], not_220_out, not_221_out, not_222_out, not_223_out, not_224_out, not_225_out, not_226_out);
  not not_221 (not_221_out, Instruction[26]);
  not not_222 (not_222_out, Instruction[27]);
  not not_223 (not_223_out, Instruction[28]);
  not not_224 (not_224_out, Instruction[29]);
  not not_225 (not_225_out, Instruction[30]);
  not not_226 (not_226_out, Instruction[31]);
  not not_227 (not_227_out, Instruction[0]);
  not not_228 (not_228_out, Instruction[2]);
  not not_229 (not_229_out, Instruction[3]);
  not not_230 (not_230_out, Instruction[4]);
  not not_231 (not_231_out, Instruction[5]);
  and and_35 (rnd, not_227_out, Instruction[1], not_228_out, not_229_out, not_230_out, not_231_out, Instruction[26], Instruction[27], Instruction[28], Instruction[29], Instruction[30], Instruction[31]);
  not not_232 (not_232_out, Instruction[0]);
  not not_233 (not_233_out, Instruction[1]);
  not not_234 (not_234_out, Instruction[3]);
  not not_235 (not_235_out, Instruction[4]);
  not not_236 (not_236_out, Instruction[5]);
  and and_36 (kbd, not_232_out, not_233_out, Instruction[2], not_234_out, not_235_out, not_236_out, Instruction[26], Instruction[27], Instruction[28], Instruction[29], Instruction[30], Instruction[31]);
  and and_37 (halt, Instruction[0], Instruction[1], Instruction[2], Instruction[3], Instruction[4], Instruction[5], Instruction[26], Instruction[27], Instruction[28], Instruction[29], Instruction[30], Instruction[31]);
  not not_237 (not_237_out, Instruction[1]);
  not not_238 (not_238_out, Instruction[2]);
  not not_239 (not_239_out, Instruction[3]);
  not not_240 (not_240_out, Instruction[4]);
  not not_241 (not_241_out, Instruction[5]);
  and and_38 (tty, Instruction[0], not_237_out, not_238_out, not_239_out, not_240_out, not_241_out, Instruction[26], Instruction[27], Instruction[28], Instruction[29], Instruction[30], Instruction[31]);
  or or_18 (EnabledHL, mul, mulu, div, divu);
  or or_19 (RW, add, sub, slt, sltu, \and , \or , \nor , \xor , addi, slti, sltiu, andi, ori, xori, lw, pop, mfhi, mflo, rnd, kbd);
  or or_20 (minus_RW, sw, push);

  // Other names for the same wires on the sheet: clk = Clock; Const[15:0] = Instruction[15:0];
  //   func_code[5:0] = Instruction[5:0]; x[4:0] = Instruction[10:6]; r0[4:0] = Instruction[15:11]; EHL = EnabledHL;
  //   instadd = add; instaddi = addi; instand = \and ; instandi = andi; instlw = lw; instor = \or ; instori = ori;
  //   instpop = pop; instpush = push; r1[4:0] = Instruction[20:16]; r2[4:0] = Instruction[25:21];
  //   op_code[5:0] = Instruction[31:26]; instslt = slt; instslti = slti; instsltiu = sltiu; instsltu = sltu;
  //   instsub = sub; instsw = sw; instxor = \xor ; instxori = xori

  // Notes on the sheet:
  //   add
  //   addi
  //   lw
  //   sw
  //   mul
  //   beq
  //   bne
  //   INPUT
  //   pop
  //   sub
  //   push
  //   blez
  //   Registers Selectors
  //   bgtz
  //   bltz
  //   mulu
  //   div
  //   divu
  //   slt
  //   slti
  //   sltu
  //   sltiu
  //   jr
  //   Identificar las Op(instrucciones)
  //   nop
  //   j
  //   and
  //   andi
  //   or
  //   ori
  //   nor
  //   xor
  //   xori
  //   OUTPUT
  //   mfhi
  //   mflo
  //   rnd
  //   kbd
  //   halt
  //   tty
  //   Operaciones
endmodule

module RAM_Manager (
  input  [31:0] Address,
  input  [31:0] RAM_Out_0,
  input  [31:0] RAM_Out_1,
  input  [31:0] RAM_Out_2,
  input  [31:0] RAM_Out_3,
  input  [31:0] Rt,
  input  [3:0] Read_Time,
  input  [3:0] Write_Time,
  input  Selector_RT,
  input  Selector_WT,
  input  sw,
  input  Clock,
  output [15:0] Address_2,
  output [31:0] RAM_In_0,
  output [31:0] RAM_In_1,
  output [31:0] RAM_In_2,
  output [31:0] RAM_In_3,
  output [3:0] Mask,
  output [31:0] Out_Value,
  output RT__0,
  output WT__0
);

  wire and_1_out, and_2_out, and_3_out, and_4_out, priority_encoder_1_en_out, priority_encoder_2_en_out;
  wire [1:0] multiplexer_3_out, multiplexer_5_out, priority_encoder_1_out, priority_encoder_2_out;
  wire [3:0] multiplexer_1_out, multiplexer_2_out, RT_1, RT_t, WT, WT_1;
  wire [19:0] divider_1_rem, divider_2_out, divider_4_rem, subtractor_3_out;
  wire [19:16] divider_3_out;
  wire [31:0] multiplexer_6_out, multiplexer_7_out, multiplexer_8_out, multiplexer_9_out, RAM_INPUT_0,
       RAM_INPUT_1, RAM_INPUT_2, RAM_INPUT_3, RAM_OUTPUT_0, RAM_OUTPUT_1, RAM_OUTPUT_2, RAM_OUTPUT_3;

  Multiplexer #(.width(4), .enable("false")) multiplexer_1 (
    .in0(Read_Time), .in1(RT_1), .out(multiplexer_1_out), .sel(Selector_RT));
  Register #(.width(4)) register_1 (.D(multiplexer_1_out), .Q(RT_t), .clk(Clock));  // open: en, clr
  Subtractor #(.width(4)) subtractor_1 (.a(RT_t), .b(4'b0001), .out(RT_1));  // open: bin, bout
  Subtractor #(.width(4)) subtractor_2 (.a(WT), .b(4'b0001), .out(WT_1));  // open: bin, bout
  Comparator #(.width(4), .mode("unsigned")) comparator_1 (.a(RT_t), .b(4'b0000), .eq(RT__0));  // open: gt, lt
  Comparator #(.width(4), .mode("unsigned")) comparator_2 (.a(WT), .b(4'b0000), .eq(WT__0));  // open: gt, lt
  Divider #(.width(20)) divider_1 (.a(Address[19:0]), .b(20'h4), .rem(divider_1_rem));  // open: out, upper
  Multiplexer #(.width(4), .enable("false")) multiplexer_2 (
    .in0(Write_Time), .in1(WT_1), .out(multiplexer_2_out), .sel(Selector_WT));
  Subtractor #(.width(20)) subtractor_3 (
    .a(Address[19:0]), .b(divider_1_rem), .out(subtractor_3_out));  // open: bin, bout
  Register #(.width(4)) register_2 (.D(multiplexer_2_out), .Q(WT), .clk(Clock));  // open: en, clr
  Priority_Encoder #(.select(2)) priority_encoder_1 (
    .in0(Mask[0]), .in1(Mask[1]), .in2(Mask[2]), .in3(Mask[3]), .out(priority_encoder_1_out),
    .en_out(priority_encoder_1_en_out));  // open: gs, en_in
  Divider #(.width(20)) divider_2 (.a(subtractor_3_out), .b(20'h4), .out(divider_2_out));  // open: upper, rem
  Demultiplexer #(.select(2), .width(32), .enable("false")) demultiplexer_1 (
    .out0(RAM_INPUT_0), .out1(RAM_INPUT_1), .out2(RAM_INPUT_2), .out3(RAM_INPUT_3), .in(Rt),
    .sel(multiplexer_3_out));
  Multiplexer #(.width(2), .enable("false")) multiplexer_3 (
    .in0(priority_encoder_1_out), .in1(2'b00), .out(multiplexer_3_out), .sel(priority_encoder_1_en_out));
  Priority_Encoder #(.select(2)) priority_encoder_2 (
    .in0(Mask[0]), .in1(Mask[1]), .in2(Mask[2]), .in3(Mask[3]), .out(priority_encoder_2_out),
    .en_out(priority_encoder_2_en_out));  // open: gs, en_in
  Divider #(.width(20)) divider_3 (
    .a(subtractor_3_out), .b(20'h10), .out({divider_3_out, Address_2}));  // open: upper, rem
  Demultiplexer #(.select(2), .enable("false")) demultiplexer_2 (
    .out0(Mask[0]), .out1(Mask[1]), .out2(Mask[2]), .out3(Mask[3]), .in(1'b1), .sel(divider_4_rem[1:0]));
  Divider #(.width(20)) divider_4 (.a(divider_2_out), .b(20'h4), .rem(divider_4_rem));  // open: out, upper
  Little_Endian little_endian_1 (.in_1(RAM_Out_0), .out_2(RAM_OUTPUT_0));
  Little_Endian little_endian_2 (.in_1(RAM_Out_1), .out_2(RAM_OUTPUT_1));
  Little_Endian little_endian_3 (.in_1(RAM_Out_2), .out_2(RAM_OUTPUT_2));
  Little_Endian little_endian_4 (.in_1(RAM_Out_3), .out_2(RAM_OUTPUT_3));
  Multiplexer #(.select(2), .width(32), .enable("false")) multiplexer_4 (
    .in0(RAM_OUTPUT_0), .in1(RAM_OUTPUT_1), .in2(RAM_OUTPUT_2), .in3(RAM_OUTPUT_3), .out(Out_Value),
    .sel(multiplexer_5_out));
  Multiplexer #(.width(2), .enable("false")) multiplexer_5 (
    .in0(priority_encoder_2_out), .in1(2'b00), .out(multiplexer_5_out), .sel(priority_encoder_2_en_out));
  Multiplexer #(.width(32), .enable("false")) multiplexer_6 (
    .in0({32{1'b0}}), .in1(RAM_INPUT_0), .out(multiplexer_6_out), .sel(and_1_out));
  Little_Endian little_endian_5 (.in_1(multiplexer_6_out), .out_2(RAM_In_0));
  Little_Endian little_endian_6 (.in_1(multiplexer_7_out), .out_2(RAM_In_1));
  Multiplexer #(.width(32), .enable("false")) multiplexer_7 (
    .in0({32{1'b0}}), .in1(RAM_INPUT_1), .out(multiplexer_7_out), .sel(and_2_out));
  Little_Endian little_endian_7 (.in_1(multiplexer_8_out), .out_2(RAM_In_2));
  Multiplexer #(.width(32), .enable("false")) multiplexer_8 (
    .in0({32{1'b0}}), .in1(RAM_INPUT_2), .out(multiplexer_8_out), .sel(and_3_out));
  Multiplexer #(.width(32), .enable("false")) multiplexer_9 (
    .in0({32{1'b0}}), .in1(RAM_INPUT_3), .out(multiplexer_9_out), .sel(and_4_out));
  Little_Endian little_endian_8 (.in_1(multiplexer_9_out), .out_2(RAM_In_3));
  and and_1 (and_1_out, Mask[0], sw);
  and and_2 (and_2_out, Mask[1], sw);
  and and_3 (and_3_out, Mask[2], sw);
  and and_4 (and_4_out, Mask[3], sw);

  // Other names for the same wires on the sheet: Line[15:0] = Address_2; Bank[3:0] = Mask; clk = Clock;
  //   SRT = Selector_RT; SWT = Selector_WT

  // Notes on the sheet:
  //   RAM TIMING
  //   DATA FROM RAM
  //   RAM ADDRESS
  //   DATA TO RAM
  //   DATA WRITE MASK
endmodule

module Branch_Control (
  input  [31:0] Current_Address_Instruction,
  input  [31:0] K,
  input  [31:0] Current_Inst,
  input  [31:0] Jump_Register,
  input  jmp,
  input  FC,
  input  JMP_Inst,
  input  JR_Inst,
  output [31:0] out_9
);

  wire and_1_out, priority_encoder_1_en_out;
  wire [1:0] multiplexer_1_out, priority_encoder_1_out;
  wire [31:0] adder_1_out, adder_2_out;

  and and_1 (and_1_out, jmp, FC);
  Adder #(.width(32)) adder_1 (.a(32'h4), .b(Current_Address_Instruction), .out(adder_1_out));  // open: cin, cout
  Adder #(.width(32)) adder_2 (.a(Current_Address_Instruction), .b(K), .out(adder_2_out));  // open: cin, cout
  Priority_Encoder #(.select(2)) priority_encoder_1 (
    .in1(and_1_out), .in2(JMP_Inst), .in3(JR_Inst), .out(priority_encoder_1_out),
    .en_out(priority_encoder_1_en_out));  // open: in0, gs, en_in
  Multiplexer #(.width(2), .enable("false")) multiplexer_1 (
    .in0(priority_encoder_1_out), .in1(2'b00), .out(multiplexer_1_out), .sel(priority_encoder_1_en_out));
  Multiplexer #(.select(2), .width(32), .enable("false")) multiplexer_2 (
    .in0(adder_1_out), .in1(adder_2_out),
    .in2({Current_Address_Instruction[31:28], Current_Inst[25:0], 2'b00}), .in3(Jump_Register), .out(out_9),
    .sel(multiplexer_1_out));

  // Notes on the sheet:
  //   INPUTS:
  //   OUTPUT:
endmodule

module _32_Registers_of_32_bits (
  input  in_1,
  input  [31:0] A,
  input  in_3,
  input  Clock,
  input  Reset,
  input  in_6,
  input  in_7,
  input  in_8,
  input  in_9,
  input  in_10,
  input  in_11,
  input  in_12,
  input  in_13,
  input  in_14,
  input  in_15,
  input  in_16,
  input  in_17,
  input  in_18,
  input  in_19,
  input  in_20,
  input  in_21,
  input  in_22,
  input  in_23,
  input  in_24,
  input  in_25,
  input  in_26,
  input  in_27,
  input  in_28,
  input  in_29,
  input  in_30,
  input  in_31,
  input  in_32,
  input  in_33,
  input  in_34,
  output [31:0] out_35,
  output [31:0] out_36,
  output [31:0] out_37,
  output [31:0] out_38,
  output [31:0] out_39,
  output [31:0] out_40,
  output [31:0] out_41,
  output [31:0] out_42,
  output [31:0] out_43,
  output [31:0] out_44,
  output [31:0] out_45,
  output [31:0] out_46,
  output [31:0] out_47,
  output [31:0] out_48,
  output [31:0] out_49,
  output [31:0] out_50,
  output [31:0] out_51,
  output [31:0] out_52,
  output [31:0] out_53,
  output [31:0] out_54,
  output [31:0] out_55,
  output [31:0] out_56,
  output [31:0] out_57,
  output [31:0] out_58,
  output [31:0] out_59,
  output [31:0] out_60,
  output [31:0] out_61,
  output [31:0] out_62,
  output [31:0] out_63,
  output [31:0] out_64,
  output [31:0] out_65
);

  Register #(.width(32)) register_1 (.D({32{1'b0}}), .en(in_1), .Q(out_35), .clk(Clock), .clr(Reset));
  Register #(.width(32)) register_2 (.D(A), .en(in_3), .Q(out_36), .clk(Clock), .clr(Reset));
  Register #(.width(32)) register_3 (.D(A), .en(in_6), .Q(out_37), .clk(Clock), .clr(Reset));
  Register #(.width(32)) register_4 (.D(A), .en(in_7), .Q(out_38), .clk(Clock), .clr(Reset));
  Register #(.width(32)) register_5 (.D(A), .en(in_8), .Q(out_39), .clk(Clock), .clr(Reset));
  Register #(.width(32)) register_6 (.D(A), .en(in_9), .Q(out_40), .clk(Clock), .clr(Reset));
  Register #(.width(32)) register_7 (.D(A), .en(in_10), .Q(out_41), .clk(Clock), .clr(Reset));
  Register #(.width(32)) register_8 (.D(A), .en(in_11), .Q(out_42), .clk(Clock), .clr(Reset));
  Register #(.width(32)) register_9 (.D(A), .en(in_12), .Q(out_43), .clk(Clock), .clr(Reset));
  Register #(.width(32)) register_10 (.D(A), .en(in_13), .Q(out_44), .clk(Clock), .clr(Reset));
  Register #(.width(32)) register_11 (.D(A), .en(in_14), .Q(out_45), .clk(Clock), .clr(Reset));
  Register #(.width(32)) register_12 (.D(A), .en(in_15), .Q(out_46), .clk(Clock), .clr(Reset));
  Register #(.width(32)) register_13 (.D(A), .en(in_16), .Q(out_47), .clk(Clock), .clr(Reset));
  Register #(.width(32)) register_14 (.D(A), .en(in_17), .Q(out_48), .clk(Clock), .clr(Reset));
  Register #(.width(32)) register_15 (.D(A), .en(in_18), .Q(out_49), .clk(Clock), .clr(Reset));
  Register #(.width(32)) register_16 (.D(A), .en(in_19), .Q(out_50), .clk(Clock), .clr(Reset));
  Register #(.width(32)) register_17 (.D(A), .en(in_20), .Q(out_51), .clk(Clock), .clr(Reset));
  Register #(.width(32)) register_18 (.D(A), .en(in_21), .Q(out_52), .clk(Clock), .clr(Reset));
  Register #(.width(32)) register_19 (.D(A), .en(in_22), .Q(out_53), .clk(Clock), .clr(Reset));
  Register #(.width(32)) register_20 (.D(A), .en(in_23), .Q(out_54), .clk(Clock), .clr(Reset));
  Register #(.width(32)) register_21 (.D(A), .en(in_24), .Q(out_55), .clk(Clock), .clr(Reset));
  Register #(.width(32)) register_22 (.D(A), .en(in_25), .Q(out_56), .clk(Clock), .clr(Reset));
  Register #(.width(32)) register_23 (.D(A), .en(in_26), .Q(out_57), .clk(Clock), .clr(Reset));
  Register #(.width(32)) register_24 (.D(A), .en(in_27), .Q(out_58), .clk(Clock), .clr(Reset));
  Register #(.width(32)) register_25 (.D(A), .en(in_28), .Q(out_59), .clk(Clock), .clr(Reset));
  Register #(.width(32)) register_26 (.D(A), .en(in_29), .Q(out_60), .clk(Clock), .clr(Reset));
  Register #(.width(32)) register_27 (.D(A), .en(in_30), .Q(out_61), .clk(Clock), .clr(Reset));
  Register #(.width(32)) register_28 (.D(A), .en(in_31), .Q(out_62), .clk(Clock), .clr(Reset));
  Register #(.width(32)) register_29 (.D(A), .en(in_32), .Q(out_63), .clk(Clock), .clr(Reset));
  Register #(.width(32)) register_30 (.D(A), .en(in_33), .Q(out_64), .clk(Clock), .clr(Reset));
  Register #(.width(32)) register_31 (.D(A), .en(in_34), .Q(out_65), .clk(Clock), .clr(Reset));

  // Other names for the same wires on the sheet: CLK = Clock
endmodule

module Select_RW (
  input  in_1,
  input  in_2,
  input  in_3,
  input  in_4,
  input  in_5,
  input  in_6,
  input  in_7,
  input  in_8,
  input  in_9,
  input  in_10,
  input  in_11,
  input  in_12,
  input  in_13,
  input  in_14,
  input  in_15,
  input  in_16,
  input  in_17,
  input  in_18,
  input  in_19,
  input  in_20,
  input  in_21,
  input  in_22,
  input  in_23,
  input  in_24,
  input  in_25,
  input  in_26,
  input  in_27,
  input  in_28,
  input  in_29,
  input  in_30,
  input  in_31,
  input  in_32,
  input  RW,
  output out_34,
  output out_35,
  output out_36,
  output out_37,
  output out_38,
  output out_39,
  output out_40,
  output out_41,
  output out_42,
  output out_43,
  output out_44,
  output out_45,
  output out_46,
  output out_47,
  output out_48,
  output out_49,
  output out_50,
  output out_51,
  output out_52,
  output out_53,
  output out_54,
  output out_55,
  output out_56,
  output out_57,
  output out_58,
  output out_59,
  output out_60,
  output out_61,
  output out_62,
  output out_63,
  output out_64,
  output out_65
);

  and and_1 (out_34, in_1, RW);
  and and_2 (out_38, in_5, RW);
  and and_3 (out_42, in_9, RW);
  and and_4 (out_46, in_13, RW);
  and and_5 (out_50, in_17, RW);
  and and_6 (out_54, in_21, RW);
  and and_7 (out_58, in_25, RW);
  and and_8 (out_62, in_29, RW);
  and and_9 (out_35, in_2, RW);
  and and_10 (out_39, in_6, RW);
  and and_11 (out_43, in_10, RW);
  and and_12 (out_47, in_14, RW);
  and and_13 (out_51, in_18, RW);
  and and_14 (out_55, in_22, RW);
  and and_15 (out_59, in_26, RW);
  and and_16 (out_63, in_30, RW);
  and and_17 (out_36, in_3, RW);
  and and_18 (out_40, in_7, RW);
  and and_19 (out_44, in_11, RW);
  and and_20 (out_48, in_15, RW);
  and and_21 (out_52, in_19, RW);
  and and_22 (out_56, in_23, RW);
  and and_23 (out_60, in_27, RW);
  and and_24 (out_64, in_31, RW);
  and and_25 (out_37, in_4, RW);
  and and_26 (out_41, in_8, RW);
  and and_27 (out_45, in_12, RW);
  and and_28 (out_49, in_16, RW);
  and and_29 (out_53, in_20, RW);
  and and_30 (out_57, in_24, RW);
  and and_31 (out_61, in_28, RW);
  and and_32 (out_65, in_32, RW);
endmodule

module Get_Operation (
  input  [5:0] func_code,
  input  [5:0] op_code,
  output out_3,
  output out_4,
  output out_5,
  output out_6
);

  wire add, \and , and_1_out, and_2_out, and_3_out, and_4_out, and_5_out, and_6_out, and_7_out, and_12_out,
       and_13_out, and_14_out, and_15_out, and_16_out, and_17_out, and_18_out, and_19_out, and_21_out,
       and_22_out, div, divu, mul, mulu, \nor , not_1_out, not_2_out, not_3_out, not_4_out, not_5_out,
       not_6_out, not_7_out, not_8_out, not_9_out, not_10_out, not_11_out, not_12_out, not_13_out,
       not_14_out, not_15_out, not_16_out, not_17_out, not_18_out, not_19_out, not_20_out, not_21_out,
       not_22_out, not_23_out, not_24_out, not_25_out, not_26_out, not_27_out, not_28_out, not_29_out,
       not_30_out, not_31_out, not_32_out, not_33_out, not_34_out, not_35_out, not_36_out, not_37_out,
       not_38_out, not_39_out, not_40_out, not_41_out, not_42_out, not_43_out, not_44_out, not_45_out,
       not_46_out, not_47_out, not_48_out, not_49_out, not_50_out, not_51_out, not_52_out, not_53_out,
       not_54_out, not_55_out, not_56_out, not_57_out, not_58_out, not_59_out, not_60_out, not_61_out,
       not_62_out, not_63_out, not_64_out, not_65_out, not_66_out, not_67_out, not_68_out, not_69_out,
       not_70_out, not_71_out, not_72_out, not_73_out, not_74_out, not_75_out, not_76_out, not_77_out,
       not_78_out, not_79_out, not_80_out, not_81_out, not_82_out, not_83_out, not_84_out, not_85_out,
       not_86_out, not_87_out, not_88_out, not_89_out, not_90_out, not_91_out, not_92_out, not_93_out,
       not_94_out, not_95_out, not_96_out, not_97_out, not_98_out, not_99_out, not_100_out, not_101_out,
       not_102_out, not_103_out, not_104_out, not_105_out, not_106_out, not_107_out, not_108_out,
       not_109_out, not_110_out, not_111_out, not_112_out, not_113_out, not_114_out, not_115_out,
       not_116_out, not_117_out, not_118_out, not_119_out, not_120_out, not_121_out, not_122_out,
       not_123_out, not_124_out, not_125_out, not_126_out, not_127_out, not_128_out, not_129_out,
       not_130_out, not_131_out, not_132_out, not_133_out, not_134_out, not_135_out, not_136_out,
       not_137_out, not_138_out, not_139_out, not_140_out, not_141_out, not_142_out, not_143_out,
       not_144_out, not_145_out, not_146_out, not_147_out, not_148_out, not_149_out, not_150_out,
       not_151_out, not_152_out, not_153_out, not_154_out, not_155_out, not_156_out, not_157_out,
       not_158_out, not_159_out, not_160_out, not_161_out, \or , slt, sltu, sub, \xor ;

  not not_1 (not_1_out, op_code[1]);
  not not_2 (not_2_out, op_code[2]);
  not not_3 (not_3_out, op_code[4]);
  not not_4 (not_4_out, op_code[5]);
  not not_5 (not_5_out, op_code[2]);
  not not_6 (not_6_out, op_code[3]);
  not not_7 (not_7_out, op_code[4]);
  not not_8 (not_8_out, op_code[2]);
  not not_9 (not_9_out, op_code[4]);
  not not_10 (not_10_out, func_code[0]);
  not not_11 (not_11_out, func_code[2]);
  not not_12 (not_12_out, func_code[3]);
  not not_13 (not_13_out, func_code[4]);
  not not_14 (not_14_out, op_code[0]);
  not not_15 (not_15_out, op_code[1]);
  not not_16 (not_16_out, op_code[2]);
  not not_17 (not_17_out, op_code[3]);
  not not_18 (not_18_out, op_code[4]);
  not not_19 (not_19_out, op_code[5]);
  not not_20 (not_20_out, func_code[1]);
  not not_21 (not_21_out, func_code[2]);
  not not_22 (not_22_out, func_code[3]);
  not not_23 (not_23_out, func_code[4]);
  not not_24 (not_24_out, func_code[5]);
  not not_25 (not_25_out, op_code[0]);
  not not_26 (not_26_out, op_code[1]);
  not not_27 (not_27_out, op_code[2]);
  not not_28 (not_28_out, func_code[0]);
  not not_29 (not_29_out, func_code[1]);
  not not_30 (not_30_out, func_code[2]);
  not not_31 (not_31_out, func_code[3]);
  not not_32 (not_32_out, func_code[4]);
  and and_1 (and_1_out, not_28_out, not_29_out, not_30_out, not_31_out, not_32_out, func_code[5], not_33_out, not_34_out, not_35_out, not_36_out, not_37_out, not_38_out);
  not not_33 (not_33_out, op_code[0]);
  not not_34 (not_34_out, op_code[1]);
  not not_35 (not_35_out, op_code[2]);
  not not_36 (not_36_out, op_code[3]);
  not not_37 (not_37_out, op_code[4]);
  not not_38 (not_38_out, op_code[5]);
  and and_2 (and_2_out, op_code[0], not_1_out, not_2_out, op_code[3], not_3_out, not_4_out);
  and and_3 (and_3_out, op_code[0], op_code[1], not_5_out, not_6_out, not_7_out, op_code[5]);
  and and_4 (and_4_out, op_code[0], op_code[1], not_8_out, op_code[3], not_9_out, op_code[5]);
  not not_39 (not_39_out, func_code[0]);
  not not_40 (not_40_out, func_code[1]);
  not not_41 (not_41_out, func_code[2]);
  not not_42 (not_42_out, func_code[3]);
  not not_43 (not_43_out, func_code[4]);
  not not_44 (not_44_out, func_code[5]);
  and and_5 (and_5_out, not_39_out, not_40_out, not_41_out, not_42_out, not_43_out, not_44_out, not_45_out, not_46_out, not_47_out, op_code[3], op_code[4], op_code[5]);
  not not_45 (not_45_out, op_code[0]);
  not not_46 (not_46_out, op_code[1]);
  not not_47 (not_47_out, op_code[2]);
  and and_6 (and_6_out, not_10_out, func_code[1], not_11_out, not_12_out, not_13_out, func_code[5], not_14_out, not_15_out, not_16_out, not_17_out, not_18_out, not_19_out);
  or or_1 (sub, and_6_out, and_7_out);
  and and_7 (and_7_out, func_code[0], not_20_out, not_21_out, not_22_out, not_23_out, not_24_out, not_25_out, not_26_out, not_27_out, op_code[3], op_code[4], op_code[5]);
  or or_2 (add, and_1_out, and_2_out, and_3_out, and_4_out, and_5_out);
  not not_48 (not_48_out, func_code[0]);
  not not_49 (not_49_out, func_code[1]);
  not not_50 (not_50_out, func_code[2]);
  not not_51 (not_51_out, func_code[5]);
  and and_8 (mul, not_48_out, not_49_out, not_50_out, func_code[3], func_code[4], not_51_out, not_52_out, not_53_out, not_54_out, not_55_out, not_56_out, not_57_out);
  not not_52 (not_52_out, op_code[0]);
  not not_53 (not_53_out, op_code[1]);
  not not_54 (not_54_out, op_code[2]);
  not not_55 (not_55_out, op_code[3]);
  not not_56 (not_56_out, op_code[4]);
  not not_57 (not_57_out, op_code[5]);
  not not_58 (not_58_out, func_code[1]);
  not not_59 (not_59_out, func_code[2]);
  not not_60 (not_60_out, func_code[5]);
  and and_9 (mulu, func_code[0], not_58_out, not_59_out, func_code[3], func_code[4], not_60_out, not_61_out, not_62_out, not_63_out, not_64_out, not_65_out, not_66_out);
  not not_61 (not_61_out, op_code[0]);
  not not_62 (not_62_out, op_code[1]);
  not not_63 (not_63_out, op_code[2]);
  not not_64 (not_64_out, op_code[3]);
  not not_65 (not_65_out, op_code[4]);
  not not_66 (not_66_out, op_code[5]);
  not not_67 (not_67_out, func_code[0]);
  not not_68 (not_68_out, func_code[2]);
  not not_69 (not_69_out, func_code[3]);
  not not_70 (not_70_out, func_code[4]);
  not not_71 (not_71_out, func_code[5]);
  and and_10 (div, not_67_out, func_code[1], not_68_out, not_69_out, not_70_out, not_71_out, not_72_out, not_73_out, not_74_out, not_75_out, not_76_out, not_77_out);
  not not_72 (not_72_out, op_code[0]);
  not not_73 (not_73_out, op_code[1]);
  not not_74 (not_74_out, op_code[2]);
  not not_75 (not_75_out, op_code[3]);
  not not_76 (not_76_out, op_code[4]);
  not not_77 (not_77_out, op_code[5]);
  not not_78 (not_78_out, func_code[2]);
  not not_79 (not_79_out, func_code[3]);
  not not_80 (not_80_out, func_code[4]);
  not not_81 (not_81_out, func_code[5]);
  and and_11 (divu, func_code[0], func_code[1], not_78_out, not_79_out, not_80_out, not_81_out, not_82_out, not_83_out, not_84_out, not_85_out, not_86_out, not_87_out);
  not not_82 (not_82_out, op_code[0]);
  not not_83 (not_83_out, op_code[1]);
  not not_84 (not_84_out, op_code[2]);
  not not_85 (not_85_out, op_code[3]);
  not not_86 (not_86_out, op_code[4]);
  not not_87 (not_87_out, op_code[5]);
  not not_88 (not_88_out, func_code[0]);
  not not_89 (not_89_out, func_code[2]);
  not not_90 (not_90_out, func_code[4]);
  not not_91 (not_91_out, op_code[0]);
  not not_92 (not_92_out, op_code[1]);
  not not_93 (not_93_out, op_code[2]);
  not not_94 (not_94_out, op_code[3]);
  not not_95 (not_95_out, op_code[4]);
  not not_96 (not_96_out, op_code[5]);
  not not_97 (not_97_out, op_code[0]);
  not not_98 (not_98_out, op_code[2]);
  not not_99 (not_99_out, op_code[4]);
  not not_100 (not_100_out, op_code[5]);
  not not_101 (not_101_out, func_code[2]);
  not not_102 (not_102_out, func_code[4]);
  and and_12 (and_12_out, func_code[0], func_code[1], not_101_out, func_code[3], not_102_out, func_code[5], not_103_out, not_104_out, not_105_out, not_106_out, not_107_out, not_108_out);
  not not_103 (not_103_out, op_code[0]);
  not not_104 (not_104_out, op_code[1]);
  not not_105 (not_105_out, op_code[2]);
  not not_106 (not_106_out, op_code[3]);
  not not_107 (not_107_out, op_code[4]);
  not not_108 (not_108_out, op_code[5]);
  not not_109 (not_109_out, op_code[2]);
  and and_13 (and_13_out, op_code[0], op_code[1], not_109_out, op_code[3], not_110_out, not_111_out);
  not not_110 (not_110_out, op_code[4]);
  not not_111 (not_111_out, op_code[5]);
  and and_14 (and_14_out, not_88_out, func_code[1], not_89_out, func_code[3], not_90_out, func_code[5], not_91_out, not_92_out, not_93_out, not_94_out, not_95_out, not_96_out);
  or or_3 (slt, and_14_out, and_15_out);
  and and_15 (and_15_out, not_97_out, op_code[1], not_98_out, op_code[3], not_99_out, not_100_out);
  or or_4 (sltu, and_12_out, and_13_out);
  not not_112 (not_112_out, func_code[0]);
  not not_113 (not_113_out, func_code[1]);
  not not_114 (not_114_out, func_code[3]);
  not not_115 (not_115_out, func_code[4]);
  not not_116 (not_116_out, op_code[0]);
  not not_117 (not_117_out, op_code[1]);
  not not_118 (not_118_out, op_code[2]);
  not not_119 (not_119_out, op_code[3]);
  not not_120 (not_120_out, op_code[4]);
  not not_121 (not_121_out, op_code[5]);
  not not_122 (not_122_out, op_code[0]);
  not not_123 (not_123_out, op_code[1]);
  not not_124 (not_124_out, op_code[4]);
  not not_125 (not_125_out, op_code[5]);
  not not_126 (not_126_out, func_code[0]);
  not not_127 (not_127_out, func_code[1]);
  not not_128 (not_128_out, func_code[3]);
  not not_129 (not_129_out, func_code[4]);
  not not_130 (not_130_out, op_code[0]);
  not not_131 (not_131_out, op_code[1]);
  not not_132 (not_132_out, op_code[2]);
  not not_133 (not_133_out, op_code[3]);
  not not_134 (not_134_out, op_code[4]);
  not not_135 (not_135_out, op_code[5]);
  not not_136 (not_136_out, op_code[1]);
  not not_137 (not_137_out, op_code[4]);
  not not_138 (not_138_out, op_code[5]);
  not not_139 (not_139_out, func_code[0]);
  not not_140 (not_140_out, func_code[1]);
  not not_141 (not_141_out, func_code[3]);
  not not_142 (not_142_out, func_code[4]);
  not not_143 (not_143_out, op_code[0]);
  not not_144 (not_144_out, op_code[1]);
  not not_145 (not_145_out, op_code[2]);
  not not_146 (not_146_out, op_code[3]);
  not not_147 (not_147_out, op_code[4]);
  not not_148 (not_148_out, op_code[5]);
  not not_149 (not_149_out, func_code[0]);
  not not_150 (not_150_out, func_code[1]);
  not not_151 (not_151_out, func_code[3]);
  not not_152 (not_152_out, func_code[4]);
  not not_153 (not_153_out, op_code[0]);
  not not_154 (not_154_out, op_code[1]);
  not not_155 (not_155_out, op_code[2]);
  not not_156 (not_156_out, op_code[3]);
  not not_157 (not_157_out, op_code[4]);
  not not_158 (not_158_out, op_code[5]);
  not not_159 (not_159_out, op_code[0]);
  not not_160 (not_160_out, op_code[4]);
  not not_161 (not_161_out, op_code[5]);
  and and_16 (and_16_out, not_112_out, not_113_out, func_code[2], not_114_out, not_115_out, func_code[5], not_116_out, not_117_out, not_118_out, not_119_out, not_120_out, not_121_out);
  or or_5 (\and , and_16_out, and_17_out);
  and and_17 (and_17_out, not_122_out, not_123_out, op_code[2], op_code[3], not_124_out, not_125_out);
  and and_18 (and_18_out, not_126_out, not_127_out, func_code[2], not_128_out, not_129_out, func_code[5], not_130_out, not_131_out, not_132_out, not_133_out, not_134_out, not_135_out);
  or or_6 (\or , and_18_out, and_19_out);
  and and_19 (and_19_out, op_code[0], not_136_out, op_code[2], op_code[3], not_137_out, not_138_out);
  and and_20 (\nor , not_139_out, not_140_out, func_code[2], not_141_out, not_142_out, func_code[5], not_143_out, not_144_out, not_145_out, not_146_out, not_147_out, not_148_out);
  and and_21 (and_21_out, not_149_out, not_150_out, func_code[2], not_151_out, not_152_out, func_code[5], not_153_out, not_154_out, not_155_out, not_156_out, not_157_out, not_158_out);
  or or_7 (\xor , and_21_out, and_22_out);
  and and_22 (and_22_out, not_159_out, op_code[1], op_code[2], op_code[3], not_160_out, not_161_out);
  Choose_Operation choose_operation_1 (
    .add(add), .sub(sub), .mul(mul), .mulu(mulu), .div(div), .divu(divu), .slt(slt), .sltu(sltu),
    .\and (\and ), .\or (\or ), .\nor (\nor ), .\xor (\xor ), .op3(out_3), .op2(out_4), .op1(out_5),
    .op0(out_6));

  // Notes on the sheet:
  //   addi
  //   sub
  //   add
  //   mul
  //   mulu
  //   div
  //   divu
  //   slt
  //   sltu
  //   and
  //   or
  //   nor
  //   xor
endmodule
module Choose_Operation (
  input  add,
  input  sub,
  input  mul,
  input  mulu,
  input  div,
  input  divu,
  input  slt,
  input  sltu,
  input  \and ,
  input  \or ,
  input  \nor ,
  input  \xor ,
  output op3,
  output op2,
  output op1,
  output op0
);

  wire and_1_out, and_2_out, and_3_out, and_4_out, and_5_out, and_6_out, and_7_out, and_8_out, and_9_out,
       and_10_out, and_11_out, and_12_out, and_13_out, and_14_out, and_15_out, and_16_out, and_17_out,
       and_18_out, and_19_out, and_20_out, and_21_out, and_22_out, and_23_out, and_24_out, and_25_out,
       and_26_out, and_27_out, and_28_out, and_29_out, and_30_out, and_31_out, and_32_out, and_33_out,
       and_34_out, and_35_out, and_36_out, and_37_out, and_38_out, and_39_out, and_40_out, and_41_out,
       and_42_out, and_43_out, and_44_out, and_45_out, and_46_out, and_47_out, and_48_out, and_49_out,
       and_50_out, and_51_out, and_52_out, and_53_out, and_54_out, and_55_out, and_56_out, and_57_out,
       and_58_out, and_59_out, and_60_out, and_61_out, and_62_out, and_63_out, and_64_out, and_65_out,
       and_66_out, and_67_out, and_68_out, and_69_out, and_70_out, not_1_out, not_2_out, not_3_out,
       not_4_out, not_5_out, not_6_out, not_7_out, not_8_out, not_9_out, not_10_out, not_11_out, not_12_out,
       not_13_out, not_14_out, not_15_out, not_16_out, not_17_out, not_18_out, not_19_out, not_20_out,
       not_21_out, not_22_out, not_23_out, not_24_out, not_25_out, not_26_out, not_27_out, not_28_out,
       not_29_out, not_30_out, not_31_out, not_32_out, not_33_out, not_34_out, not_35_out, not_36_out,
       not_37_out, not_38_out, not_39_out, not_40_out, not_41_out, not_42_out, not_43_out, not_44_out,
       not_45_out, not_46_out, not_47_out, not_48_out, not_49_out, not_50_out, not_51_out, not_52_out,
       not_53_out, not_54_out, not_55_out, not_56_out, not_57_out, not_58_out, not_59_out, not_60_out,
       not_61_out, not_62_out, not_63_out, not_64_out, not_65_out, not_66_out, not_67_out, not_68_out,
       not_69_out, not_70_out, not_71_out, not_72_out, not_73_out, not_74_out, not_75_out, not_76_out,
       not_77_out, not_78_out, not_79_out, not_80_out, not_81_out, not_82_out, not_83_out, not_84_out,
       not_85_out, not_86_out, not_87_out, not_88_out, not_89_out, not_90_out, not_91_out, not_92_out,
       not_93_out, not_94_out, not_95_out, not_96_out, not_97_out, not_98_out, not_99_out, not_100_out,
       not_101_out, not_102_out, not_103_out, not_104_out, not_105_out, not_106_out, not_107_out,
       not_108_out, not_109_out, not_110_out, not_111_out, not_112_out, not_113_out, not_114_out,
       not_115_out, not_116_out, not_117_out, not_118_out, not_119_out, not_120_out, not_121_out,
       not_122_out, not_123_out, not_124_out, not_125_out, not_126_out, not_127_out, not_128_out,
       not_129_out, not_130_out, not_131_out, not_132_out, not_133_out, not_134_out, not_135_out,
       not_136_out, not_137_out, not_138_out, not_139_out, not_140_out, not_141_out, not_142_out,
       not_143_out, not_144_out, not_145_out, not_146_out, not_147_out, not_148_out, or_3_out, or_5_out,
       or_6_out, or_8_out;

  not not_1 (not_1_out, add);
  not not_2 (not_2_out, sub);
  not not_3 (not_3_out, mul);
  not not_4 (not_4_out, mulu);
  not not_5 (not_5_out, div);
  not not_6 (not_6_out, divu);
  not not_7 (not_7_out, slt);
  not not_8 (not_8_out, sltu);
  not not_9 (not_9_out, add);
  not not_10 (not_10_out, sub);
  not not_11 (not_11_out, mul);
  not not_12 (not_12_out, mulu);
  not not_13 (not_13_out, \and );
  not not_14 (not_14_out, \or );
  not not_15 (not_15_out, \nor );
  not not_16 (not_16_out, \xor );
  not not_17 (not_17_out, add);
  not not_18 (not_18_out, sub);
  not not_19 (not_19_out, mul);
  not not_20 (not_20_out, mulu);
  not not_21 (not_21_out, div);
  not not_22 (not_22_out, divu);
  not not_23 (not_23_out, slt);
  not not_24 (not_24_out, sltu);
  not not_25 (not_25_out, \and );
  not not_26 (not_26_out, \or );
  not not_27 (not_27_out, \nor );
  not not_28 (not_28_out, add);
  not not_29 (not_29_out, sub);
  not not_30 (not_30_out, mul);
  not not_31 (not_31_out, mulu);
  not not_32 (not_32_out, div);
  not not_33 (not_33_out, divu);
  not not_34 (not_34_out, slt);
  not not_35 (not_35_out, sltu);
  not not_36 (not_36_out, \and );
  not not_37 (not_37_out, \or );
  not not_38 (not_38_out, \xor );
  not not_39 (not_39_out, add);
  not not_40 (not_40_out, sub);
  not not_41 (not_41_out, mul);
  not not_42 (not_42_out, mulu);
  not not_43 (not_43_out, div);
  not not_44 (not_44_out, divu);
  not not_45 (not_45_out, slt);
  not not_46 (not_46_out, \and );
  not not_47 (not_47_out, \or );
  not not_48 (not_48_out, \nor );
  not not_49 (not_49_out, \xor );
  not not_50 (not_50_out, add);
  not not_51 (not_51_out, sub);
  not not_52 (not_52_out, mul);
  not not_53 (not_53_out, mulu);
  not not_54 (not_54_out, div);
  not not_55 (not_55_out, divu);
  not not_56 (not_56_out, sltu);
  not not_57 (not_57_out, \and );
  not not_58 (not_58_out, \or );
  not not_59 (not_59_out, \nor );
  not not_60 (not_60_out, \xor );
  not not_61 (not_61_out, add);
  not not_62 (not_62_out, sub);
  not not_63 (not_63_out, mul);
  not not_64 (not_64_out, div);
  not not_65 (not_65_out, divu);
  not not_66 (not_66_out, slt);
  not not_67 (not_67_out, sltu);
  not not_68 (not_68_out, \and );
  not not_69 (not_69_out, \or );
  not not_70 (not_70_out, \nor );
  not not_71 (not_71_out, \xor );
  not not_72 (not_72_out, add);
  not not_73 (not_73_out, sub);
  not not_74 (not_74_out, mulu);
  not not_75 (not_75_out, div);
  not not_76 (not_76_out, divu);
  not not_77 (not_77_out, slt);
  not not_78 (not_78_out, sltu);
  not not_79 (not_79_out, \and );
  not not_80 (not_80_out, \or );
  not not_81 (not_81_out, \nor );
  not not_82 (not_82_out, \xor );
  not not_83 (not_83_out, add);
  not not_84 (not_84_out, sub);
  not not_85 (not_85_out, mul);
  not not_86 (not_86_out, mulu);
  not not_87 (not_87_out, div);
  not not_88 (not_88_out, divu);
  not not_89 (not_89_out, slt);
  not not_90 (not_90_out, sltu);
  not not_91 (not_91_out, \and );
  not not_92 (not_92_out, \or );
  not not_93 (not_93_out, \nor );
  not not_94 (not_94_out, add);
  not not_95 (not_95_out, sub);
  not not_96 (not_96_out, mul);
  not not_97 (not_97_out, mulu);
  not not_98 (not_98_out, div);
  not not_99 (not_99_out, divu);
  not not_100 (not_100_out, slt);
  not not_101 (not_101_out, sltu);
  not not_102 (not_102_out, \and );
  not not_103 (not_103_out, \nor );
  not not_104 (not_104_out, \xor );
  not not_105 (not_105_out, add);
  not not_106 (not_106_out, sub);
  not not_107 (not_107_out, mul);
  not not_108 (not_108_out, mulu);
  not not_109 (not_109_out, div);
  not not_110 (not_110_out, divu);
  not not_111 (not_111_out, slt);
  not not_112 (not_112_out, \and );
  not not_113 (not_113_out, \or );
  not not_114 (not_114_out, \nor );
  not not_115 (not_115_out, \xor );
  not not_116 (not_116_out, add);
  not not_117 (not_117_out, sub);
  not not_118 (not_118_out, mul);
  not not_119 (not_119_out, mulu);
  not not_120 (not_120_out, div);
  not not_121 (not_121_out, slt);
  not not_122 (not_122_out, sltu);
  not not_123 (not_123_out, \and );
  not not_124 (not_124_out, \or );
  not not_125 (not_125_out, \nor );
  not not_126 (not_126_out, \xor );
  not not_127 (not_127_out, add);
  not not_128 (not_128_out, sub);
  not not_129 (not_129_out, mul);
  not not_130 (not_130_out, div);
  not not_131 (not_131_out, divu);
  not not_132 (not_132_out, slt);
  not not_133 (not_133_out, sltu);
  not not_134 (not_134_out, \and );
  not not_135 (not_135_out, \or );
  not not_136 (not_136_out, \nor );
  not not_137 (not_137_out, \xor );
  not not_138 (not_138_out, add);
  not not_139 (not_139_out, mul);
  not not_140 (not_140_out, mulu);
  not not_141 (not_141_out, div);
  not not_142 (not_142_out, divu);
  not not_143 (not_143_out, slt);
  not not_144 (not_144_out, sltu);
  not not_145 (not_145_out, \and );
  not not_146 (not_146_out, \or );
  not not_147 (not_147_out, \nor );
  not not_148 (not_148_out, \xor );
  and and_1 (and_1_out, not_1_out, not_2_out, not_3_out, not_4_out, not_5_out, not_6_out, not_7_out, not_8_out);
  and and_2 (and_2_out, slt, sltu);
  and and_3 (and_3_out, divu, sltu);
  and and_4 (and_4_out, divu, slt);
  and and_5 (and_5_out, div, sltu);
  and and_6 (and_6_out, div, slt);
  and and_7 (and_7_out, div, divu);
  and and_8 (and_8_out, mulu, sltu);
  and and_9 (and_9_out, mulu, slt);
  and and_10 (and_10_out, mulu, divu);
  and and_11 (and_11_out, mulu, div);
  and and_12 (and_12_out, mul, sltu);
  and and_13 (and_13_out, mul, slt);
  and and_14 (and_14_out, mul, divu);
  and and_15 (and_15_out, mul, div);
  and and_16 (and_16_out, mul, mulu);
  and and_17 (and_17_out, sub, sltu);
  and and_18 (and_18_out, sub, slt);
  and and_19 (and_19_out, sub, divu);
  and and_20 (and_20_out, sub, div);
  and and_21 (and_21_out, sub, mulu);
  and and_22 (and_22_out, sub, mul);
  and and_23 (and_23_out, add, sltu);
  and and_24 (and_24_out, add, slt);
  and and_25 (and_25_out, add, divu);
  and and_26 (and_26_out, add, div);
  and and_27 (and_27_out, add, mulu);
  and and_28 (and_28_out, add, mul);
  and and_29 (and_29_out, add, sub);
  and and_30 (and_30_out, not_9_out, not_10_out, not_11_out, not_12_out, not_13_out, not_14_out, not_15_out, not_16_out);
  and and_31 (and_31_out, \nor , \xor );
  and and_32 (and_32_out, \or , \xor );
  and and_33 (and_33_out, \or , \nor );
  and and_34 (and_34_out, \and , \xor );
  and and_35 (and_35_out, \and , \nor );
  and and_36 (and_36_out, \and , \or );
  and and_37 (and_37_out, mulu, \xor );
  and and_38 (and_38_out, mulu, \nor );
  and and_39 (and_39_out, mulu, \or );
  and and_40 (and_40_out, mulu, \and );
  and and_41 (and_41_out, mul, \xor );
  and and_42 (and_42_out, mul, \nor );
  and and_43 (and_43_out, mul, \or );
  and and_44 (and_44_out, mul, \and );
  and and_45 (and_45_out, mul, mulu);
  and and_46 (and_46_out, sub, \xor );
  and and_47 (and_47_out, sub, \nor );
  and and_48 (and_48_out, sub, \or );
  and and_49 (and_49_out, sub, \and );
  and and_50 (and_50_out, sub, mulu);
  and and_51 (and_51_out, sub, mul);
  and and_52 (and_52_out, add, \xor );
  and and_53 (and_53_out, add, \nor );
  and and_54 (and_54_out, add, \or );
  and and_55 (and_55_out, add, \and );
  and and_56 (and_56_out, add, mulu);
  and and_57 (and_57_out, add, mul);
  and and_58 (and_58_out, add, sub);
  and and_59 (and_59_out, not_17_out, not_18_out, not_19_out, not_20_out, not_21_out, not_22_out, not_23_out, not_24_out, not_25_out, not_26_out, not_27_out, \xor );
  and and_60 (and_60_out, not_28_out, not_29_out, not_30_out, not_31_out, not_32_out, not_33_out, not_34_out, not_35_out, not_36_out, not_37_out, \nor , not_38_out);
  and and_61 (and_61_out, not_39_out, not_40_out, not_41_out, not_42_out, not_43_out, not_44_out, not_45_out, sltu, not_46_out, not_47_out, not_48_out, not_49_out);
  and and_62 (and_62_out, not_50_out, not_51_out, not_52_out, not_53_out, not_54_out, not_55_out, slt, not_56_out, not_57_out, not_58_out, not_59_out, not_60_out);
  and and_63 (and_63_out, not_61_out, not_62_out, not_63_out, mulu, not_64_out, not_65_out, not_66_out, not_67_out, not_68_out, not_69_out, not_70_out, not_71_out);
  and and_64 (and_64_out, not_72_out, not_73_out, mul, not_74_out, not_75_out, not_76_out, not_77_out, not_78_out, not_79_out, not_80_out, not_81_out, not_82_out);
  and and_65 (and_65_out, not_83_out, not_84_out, not_85_out, not_86_out, not_87_out, not_88_out, not_89_out, not_90_out, not_91_out, not_92_out, not_93_out, \xor );
  and and_66 (and_66_out, not_94_out, not_95_out, not_96_out, not_97_out, not_98_out, not_99_out, not_100_out, not_101_out, not_102_out, \or , not_103_out, not_104_out);
  and and_67 (and_67_out, not_105_out, not_106_out, not_107_out, not_108_out, not_109_out, not_110_out, not_111_out, sltu, not_112_out, not_113_out, not_114_out, not_115_out);
  and and_68 (and_68_out, not_116_out, not_117_out, not_118_out, not_119_out, not_120_out, divu, not_121_out, not_122_out, not_123_out, not_124_out, not_125_out, not_126_out);
  and and_69 (and_69_out, not_127_out, not_128_out, not_129_out, mulu, not_130_out, not_131_out, not_132_out, not_133_out, not_134_out, not_135_out, not_136_out, not_137_out);
  and and_70 (and_70_out, not_138_out, sub, not_139_out, not_140_out, not_141_out, not_142_out, not_143_out, not_144_out, not_145_out, not_146_out, not_147_out, not_148_out);
  or or_1 (op1, and_59_out, and_60_out, and_61_out, and_62_out, and_63_out, and_64_out);
  or or_2 (op0, and_65_out, and_66_out, and_67_out, and_68_out, and_69_out, and_70_out);
  or or_3 (or_3_out, and_1_out, \xor , \nor , \or , \and , and_2_out, and_3_out, and_4_out, and_5_out, and_6_out, and_7_out, and_8_out, and_9_out, and_10_out, and_11_out, and_12_out, and_13_out);
  or or_4 (op3, or_3_out, or_5_out);
  or or_5 (or_5_out, and_14_out, and_15_out, and_16_out, and_17_out, and_18_out, and_19_out, and_20_out, and_21_out, and_22_out, and_23_out, and_24_out, and_25_out, and_26_out, and_27_out, and_28_out, and_29_out);
  or or_6 (or_6_out, and_30_out, and_31_out, and_32_out, and_33_out, and_34_out, and_35_out, and_36_out, sltu, slt, divu, div, and_37_out, and_38_out, and_39_out, and_40_out, and_41_out, and_42_out);
  or or_7 (op2, or_6_out, or_8_out);
  or or_8 (or_8_out, and_43_out, and_44_out, and_45_out, and_46_out, and_47_out, and_48_out, and_49_out, and_50_out, and_51_out, and_52_out, and_53_out, and_54_out, and_55_out, and_56_out, and_57_out, and_58_out);
endmodule

module MULU (
  input  [31:0] A,
  input  [31:0] B,
  output [31:0] Hi,
  output [31:0] Lo
);

  wire adder_1_cout, adder_2_cout, adder_3_cout, adder_4_cout, adder_5_cout, adder_6_cout, adder_7_cout,
       adder_9_cout, adder_10_cout, adder_11_cout, adder_12_cout, adder_13_cout, adder_14_cout,
       adder_15_cout, adder_17_cout, adder_18_cout, adder_19_cout, adder_20_cout, adder_21_cout,
       adder_22_cout, adder_23_cout, adder_25_cout, adder_26_cout, adder_27_cout, adder_28_cout,
       adder_29_cout, adder_30_cout, adder_31_cout, Carry7, Carry15, Carry23;
  wire [30:0] adder_1_out, adder_2_out, adder_3_out, adder_4_out, adder_5_out, adder_6_out, adder_7_out,
       adder_9_out, adder_10_out, adder_11_out, adder_12_out, adder_13_out, adder_14_out, adder_15_out,
       adder_17_out, adder_18_out, adder_19_out, adder_20_out, adder_21_out, adder_22_out, adder_23_out,
       adder_25_out, adder_26_out, adder_27_out, adder_28_out, adder_29_out, adder_30_out, adder_31_out;
  wire [31:0] _0, _1, _2, _3, _4, _5, _6, _7, _8, _9, _10, _11, _12, _13, _14, _15, _16, _17, _18, _19, _20,
       _21, _22, _23, _24, _25, _26, _27, _28, _29, _30, _31, and_1_out, and_2_out, and_3_out, and_4_out,
       and_5_out, and_6_out, and_7_out, and_8_out, and_9_out, and_10_out, and_11_out, and_12_out, and_13_out,
       and_14_out, and_15_out, and_16_out, and_17_out, and_18_out, and_19_out, and_20_out, and_21_out,
       and_22_out, and_23_out, and_24_out, and_25_out, and_26_out, and_27_out, and_28_out, and_29_out,
       and_30_out, and_31_out, and_32_out;
  wire [31:1] adder_8_out, adder_16_out, adder_24_out;

  assign and_1_out = A & _0;  // AND_Gate and_1, 32 bits wide
  assign and_2_out = A & _1;  // AND_Gate and_2, 32 bits wide
  assign and_3_out = A & _2;  // AND_Gate and_3, 32 bits wide
  assign and_4_out = A & _3;  // AND_Gate and_4, 32 bits wide
  assign and_5_out = A & _4;  // AND_Gate and_5, 32 bits wide
  assign and_6_out = A & _5;  // AND_Gate and_6, 32 bits wide
  assign and_7_out = A & _6;  // AND_Gate and_7, 32 bits wide
  assign and_8_out = A & _7;  // AND_Gate and_8, 32 bits wide
  Adder #(.width(32)) adder_1 (
    .a({32{1'b0}}), .b(and_1_out), .out({adder_1_out, Lo[0]}), .cout(adder_1_cout));  // open: cin
  Adder #(.width(32)) adder_2 (
    .a({1'b0, adder_1_out}), .b(and_2_out), .out({adder_2_out, Lo[1]}), .cin(adder_1_cout),
    .cout(adder_2_cout));
  Adder #(.width(32)) adder_3 (
    .a({1'b0, adder_2_out}), .b(and_3_out), .out({adder_3_out, Lo[2]}), .cin(adder_2_cout),
    .cout(adder_3_cout));
  Adder #(.width(32)) adder_4 (
    .a({1'b0, adder_3_out}), .b(and_4_out), .out({adder_4_out, Lo[3]}), .cin(adder_3_cout),
    .cout(adder_4_cout));
  Adder #(.width(32)) adder_5 (
    .a({1'b0, adder_4_out}), .b(and_5_out), .out({adder_5_out, Lo[4]}), .cin(adder_4_cout),
    .cout(adder_5_cout));
  Adder #(.width(32)) adder_6 (
    .a({1'b0, adder_5_out}), .b(and_6_out), .out({adder_6_out, Lo[5]}), .cin(adder_5_cout),
    .cout(adder_6_cout));
  Adder #(.width(32)) adder_7 (
    .a({1'b0, adder_6_out}), .b(and_7_out), .out({adder_7_out, Lo[6]}), .cin(adder_6_cout),
    .cout(adder_7_cout));
  Adder #(.width(32)) adder_8 (
    .a({1'b0, adder_7_out}), .b(and_8_out), .out({adder_8_out, Lo[7]}), .cin(adder_7_cout), .cout(Carry7));
  assign _0 = {{31{B[0]}}, B[0]};  // Bit_Extender bit_extender_1
  assign _1 = {{31{B[1]}}, B[1]};  // Bit_Extender bit_extender_2
  assign _2 = {{31{B[2]}}, B[2]};  // Bit_Extender bit_extender_3
  assign _3 = {{31{B[3]}}, B[3]};  // Bit_Extender bit_extender_4
  assign _4 = {{31{B[4]}}, B[4]};  // Bit_Extender bit_extender_5
  assign _5 = {{31{B[5]}}, B[5]};  // Bit_Extender bit_extender_6
  assign _6 = {{31{B[6]}}, B[6]};  // Bit_Extender bit_extender_7
  assign _7 = {{31{B[7]}}, B[7]};  // Bit_Extender bit_extender_8
  assign and_9_out = A & _8;  // AND_Gate and_9, 32 bits wide
  assign and_10_out = A & _9;  // AND_Gate and_10, 32 bits wide
  assign and_11_out = A & _10;  // AND_Gate and_11, 32 bits wide
  assign and_12_out = A & _11;  // AND_Gate and_12, 32 bits wide
  assign and_13_out = A & _12;  // AND_Gate and_13, 32 bits wide
  assign and_14_out = A & _13;  // AND_Gate and_14, 32 bits wide
  assign and_15_out = A & _14;  // AND_Gate and_15, 32 bits wide
  assign and_16_out = A & _15;  // AND_Gate and_16, 32 bits wide
  Adder #(.width(32)) adder_9 (
    .a({1'b0, adder_8_out}), .b(and_9_out), .out({adder_9_out, Lo[8]}), .cin(Carry7), .cout(adder_9_cout));
  Adder #(.width(32)) adder_10 (
    .a({1'b0, adder_9_out}), .b(and_10_out), .out({adder_10_out, Lo[9]}), .cin(adder_9_cout),
    .cout(adder_10_cout));
  Adder #(.width(32)) adder_11 (
    .a({1'b0, adder_10_out}), .b(and_11_out), .out({adder_11_out, Lo[10]}), .cin(adder_10_cout),
    .cout(adder_11_cout));
  Adder #(.width(32)) adder_12 (
    .a({1'b0, adder_11_out}), .b(and_12_out), .out({adder_12_out, Lo[11]}), .cin(adder_11_cout),
    .cout(adder_12_cout));
  Adder #(.width(32)) adder_13 (
    .a({1'b0, adder_12_out}), .b(and_13_out), .out({adder_13_out, Lo[12]}), .cin(adder_12_cout),
    .cout(adder_13_cout));
  Adder #(.width(32)) adder_14 (
    .a({1'b0, adder_13_out}), .b(and_14_out), .out({adder_14_out, Lo[13]}), .cin(adder_13_cout),
    .cout(adder_14_cout));
  Adder #(.width(32)) adder_15 (
    .a({1'b0, adder_14_out}), .b(and_15_out), .out({adder_15_out, Lo[14]}), .cin(adder_14_cout),
    .cout(adder_15_cout));
  Adder #(.width(32)) adder_16 (
    .a({1'b0, adder_15_out}), .b(and_16_out), .out({adder_16_out, Lo[15]}), .cin(adder_15_cout),
    .cout(Carry15));
  assign _8 = {{31{B[8]}}, B[8]};  // Bit_Extender bit_extender_9
  assign _9 = {{31{B[9]}}, B[9]};  // Bit_Extender bit_extender_10
  assign _10 = {{31{B[10]}}, B[10]};  // Bit_Extender bit_extender_11
  assign _11 = {{31{B[11]}}, B[11]};  // Bit_Extender bit_extender_12
  assign _12 = {{31{B[12]}}, B[12]};  // Bit_Extender bit_extender_13
  assign _13 = {{31{B[13]}}, B[13]};  // Bit_Extender bit_extender_14
  assign _14 = {{31{B[14]}}, B[14]};  // Bit_Extender bit_extender_15
  assign _15 = {{31{B[15]}}, B[15]};  // Bit_Extender bit_extender_16
  assign and_17_out = A & _16;  // AND_Gate and_17, 32 bits wide
  assign and_18_out = A & _17;  // AND_Gate and_18, 32 bits wide
  assign and_19_out = A & _18;  // AND_Gate and_19, 32 bits wide
  assign and_20_out = A & _19;  // AND_Gate and_20, 32 bits wide
  assign and_21_out = A & _20;  // AND_Gate and_21, 32 bits wide
  assign and_22_out = A & _21;  // AND_Gate and_22, 32 bits wide
  assign and_23_out = A & _22;  // AND_Gate and_23, 32 bits wide
  assign and_24_out = A & _23;  // AND_Gate and_24, 32 bits wide
  assign _16 = {{31{B[16]}}, B[16]};  // Bit_Extender bit_extender_17
  assign _17 = {{31{B[17]}}, B[17]};  // Bit_Extender bit_extender_18
  assign _18 = {{31{B[18]}}, B[18]};  // Bit_Extender bit_extender_19
  assign _19 = {{31{B[19]}}, B[19]};  // Bit_Extender bit_extender_20
  assign _20 = {{31{B[20]}}, B[20]};  // Bit_Extender bit_extender_21
  assign _21 = {{31{B[21]}}, B[21]};  // Bit_Extender bit_extender_22
  assign _22 = {{31{B[22]}}, B[22]};  // Bit_Extender bit_extender_23
  assign _23 = {{31{B[23]}}, B[23]};  // Bit_Extender bit_extender_24
  Adder #(.width(32)) adder_17 (
    .a({1'b0, adder_16_out}), .b(and_17_out), .out({adder_17_out, Lo[16]}), .cin(Carry15),
    .cout(adder_17_cout));
  Adder #(.width(32)) adder_18 (
    .a({1'b0, adder_17_out}), .b(and_18_out), .out({adder_18_out, Lo[17]}), .cin(adder_17_cout),
    .cout(adder_18_cout));
  Adder #(.width(32)) adder_19 (
    .a({1'b0, adder_18_out}), .b(and_19_out), .out({adder_19_out, Lo[18]}), .cin(adder_18_cout),
    .cout(adder_19_cout));
  Adder #(.width(32)) adder_20 (
    .a({1'b0, adder_19_out}), .b(and_20_out), .out({adder_20_out, Lo[19]}), .cin(adder_19_cout),
    .cout(adder_20_cout));
  Adder #(.width(32)) adder_21 (
    .a({1'b0, adder_20_out}), .b(and_21_out), .out({adder_21_out, Lo[20]}), .cin(adder_20_cout),
    .cout(adder_21_cout));
  Adder #(.width(32)) adder_22 (
    .a({1'b0, adder_21_out}), .b(and_22_out), .out({adder_22_out, Lo[21]}), .cin(adder_21_cout),
    .cout(adder_22_cout));
  Adder #(.width(32)) adder_23 (
    .a({1'b0, adder_22_out}), .b(and_23_out), .out({adder_23_out, Lo[22]}), .cin(adder_22_cout),
    .cout(adder_23_cout));
  Adder #(.width(32)) adder_24 (
    .a({1'b0, adder_23_out}), .b(and_24_out), .out({adder_24_out, Lo[23]}), .cin(adder_23_cout),
    .cout(Carry23));
  assign _24 = {{31{B[24]}}, B[24]};  // Bit_Extender bit_extender_25
  assign _25 = {{31{B[25]}}, B[25]};  // Bit_Extender bit_extender_26
  assign _26 = {{31{B[26]}}, B[26]};  // Bit_Extender bit_extender_27
  assign _27 = {{31{B[27]}}, B[27]};  // Bit_Extender bit_extender_28
  assign _28 = {{31{B[28]}}, B[28]};  // Bit_Extender bit_extender_29
  assign _29 = {{31{B[29]}}, B[29]};  // Bit_Extender bit_extender_30
  assign _30 = {{31{B[30]}}, B[30]};  // Bit_Extender bit_extender_31
  assign _31 = {{31{B[31]}}, B[31]};  // Bit_Extender bit_extender_32
  assign and_25_out = A & _24;  // AND_Gate and_25, 32 bits wide
  assign and_26_out = A & _25;  // AND_Gate and_26, 32 bits wide
  assign and_27_out = A & _26;  // AND_Gate and_27, 32 bits wide
  assign and_28_out = A & _27;  // AND_Gate and_28, 32 bits wide
  assign and_29_out = A & _28;  // AND_Gate and_29, 32 bits wide
  assign and_30_out = A & _29;  // AND_Gate and_30, 32 bits wide
  assign and_31_out = A & _30;  // AND_Gate and_31, 32 bits wide
  assign and_32_out = A & _31;  // AND_Gate and_32, 32 bits wide
  Adder #(.width(32)) adder_25 (
    .a({1'b0, adder_24_out}), .b(and_25_out), .out({adder_25_out, Lo[24]}), .cin(Carry23),
    .cout(adder_25_cout));
  Adder #(.width(32)) adder_26 (
    .a({1'b0, adder_25_out}), .b(and_26_out), .out({adder_26_out, Lo[25]}), .cin(adder_25_cout),
    .cout(adder_26_cout));
  Adder #(.width(32)) adder_27 (
    .a({1'b0, adder_26_out}), .b(and_27_out), .out({adder_27_out, Lo[26]}), .cin(adder_26_cout),
    .cout(adder_27_cout));
  Adder #(.width(32)) adder_28 (
    .a({1'b0, adder_27_out}), .b(and_28_out), .out({adder_28_out, Lo[27]}), .cin(adder_27_cout),
    .cout(adder_28_cout));
  Adder #(.width(32)) adder_29 (
    .a({1'b0, adder_28_out}), .b(and_29_out), .out({adder_29_out, Lo[28]}), .cin(adder_28_cout),
    .cout(adder_29_cout));
  Adder #(.width(32)) adder_30 (
    .a({1'b0, adder_29_out}), .b(and_30_out), .out({adder_30_out, Lo[29]}), .cin(adder_29_cout),
    .cout(adder_30_cout));
  Adder #(.width(32)) adder_31 (
    .a({1'b0, adder_30_out}), .b(and_31_out), .out({adder_31_out, Lo[30]}), .cin(adder_30_cout),
    .cout(adder_31_cout));
  Adder #(.width(32)) adder_32 (
    .a({1'b0, adder_31_out}), .b(and_32_out), .out({Hi[30:0], Lo[31]}), .cin(adder_31_cout), .cout(Hi[31]));

  // Other names for the same wires on the sheet: Carry21 = Hi[31]; O0 = Lo[0]; O1 = Lo[1]; O2 = Lo[2]; O3 = Lo[3];
  //   O4 = Lo[4]; O5 = Lo[5]; O6 = Lo[6]; O7 = Lo[7]; O8 = Lo[8]; O9 = Lo[9]; O10 = Lo[10]; O11 = Lo[11];
  //   O12 = Lo[12]; O13 = Lo[13]; O14 = Lo[14]; O15 = Lo[15]; O16 = Lo[16]; O17 = Lo[17]; O18 = Lo[18]; O19 = Lo[19];
  //   O20 = Lo[20]; O21 = Lo[21]; O22 = Lo[22]; O23 = Lo[23]; O24 = Lo[24]; O25 = Lo[25]; O26 = Lo[26]; O27 = Lo[27];
  //   O28 = Lo[28]; O29 = Lo[29]; O30 = Lo[30]; O31 = Lo[31]

  // Notes on the sheet:
  //   INPUT:
  //   OUTPUT:
endmodule

module S_DIV (
  input  [31:0] A,
  input  [31:0] B,
  output [31:0] Lo,
  output [31:0] Hi
);

  wire comparator_1_lt, xor_1_out, xor_2_out;
  wire [31:0] adder_1_out, adder_2_out, adder_3_out, adder_4_out, divider_1_out, divider_1_rem,
       multiplexer_1_out, multiplexer_2_out, multiplexer_3_out, multiplier_1_out, not_1_out, not_2_out,
       not_3_out, not_4_out;

  assign not_1_out = ~A;  // NOT_Gate not_1, 32 bits wide
  Adder #(.width(32)) adder_1 (.a(not_1_out), .b(32'h1), .out(adder_1_out));  // open: cin, cout
  assign not_2_out = ~B;  // NOT_Gate not_2, 32 bits wide
  Adder #(.width(32)) adder_2 (.a(not_2_out), .b(32'h1), .out(adder_2_out));  // open: cin, cout
  Multiplexer #(.width(32), .enable("false")) multiplexer_1 (
    .in0(A), .in1(adder_1_out), .out(multiplexer_1_out), .sel(A[31]));
  Multiplexer #(.width(32), .enable("false")) multiplexer_2 (
    .in0(B), .in1(adder_2_out), .out(multiplexer_2_out), .sel(B[31]));
  Divider #(.width(32)) divider_1 (
    .a(multiplexer_1_out), .b(multiplexer_2_out), .out(divider_1_out), .rem(divider_1_rem));  // open: upper
  assign not_3_out = ~divider_1_rem;  // NOT_Gate not_3, 32 bits wide
  xor xor_1 (xor_1_out, B[31], A[31]);
  Adder #(.width(32)) adder_3 (.a(not_3_out), .b(32'h1), .out(adder_3_out));  // open: cin, cout
  assign not_4_out = ~divider_1_out;  // NOT_Gate not_4, 32 bits wide
  Adder #(.width(32)) adder_4 (.a(not_4_out), .b(32'h1), .out(adder_4_out));  // open: cin, cout
  Multiplexer #(.width(32), .enable("false")) multiplexer_3 (
    .in0(divider_1_rem), .in1(adder_3_out), .out(multiplexer_3_out), .sel(xor_1_out));
  Multiplexer #(.width(32), .enable("false")) multiplexer_4 (
    .in0(divider_1_out), .in1(adder_4_out), .out(Lo), .sel(xor_2_out));
  xor xor_2 (xor_2_out, B[31], A[31]);
  Multiplier #(.width(32)) multiplier_1 (
    .a(multiplexer_3_out), .b({32{1'b1}}), .out(multiplier_1_out));  // open: cin, cout
  Comparator #(.width(32)) comparator_1 (.a(multiplexer_3_out), .b({32{1'b0}}), .lt(comparator_1_lt));  // open: gt, eq
  Multiplexer #(.width(32), .enable("false")) multiplexer_5 (
    .in0(multiplexer_3_out), .in1(multiplier_1_out), .out(Hi), .sel(comparator_1_lt));

  // Other names for the same wires on the sheet: S_prime_prime = B[31]; S_prime = A[31]

  // Notes on the sheet:
  //   INPUT:
  //   OUTPUT:
endmodule

module Little_Endian (
  input  [31:0] in_1,
  output [31:0] out_2
);


  assign out_2 = {in_1[7:0], in_1[15:8], in_1[23:16], in_1[31:24]};

  // Other names for the same wires on the sheet: _24_31[7:0] = in_1[31:24]; _16_23[7:0] = in_1[23:16];
  //   _8_15[7:0] = in_1[15:8]; _0_7[7:0] = in_1[7:0]
endmodule
